// Digital circuit 32-bit Fibonacci_generator_1.dig as structural Verilog
module _32_bit_Fibonacci_generator_1 (
  input  clk,
  input  in_2,
  input  in_3,
  input  in_4,
  input  A,
  input  in_11,
  output LD,
  output RES,
  output GCLK,
  output T0,
  output RST
);

  wire _74161_1_pin15, ADD, AND, Aout, Bout, button_1_out, button_2_out, C, Cin, CLA, CLR, Cout, D0, D1, D2,
       D3, D4, D5, D6, D7, D8, D9, D10, D11, D12, D13, D14, D15, D16, D17, D18, D19, D20, D21, D22, D23, D24,
       D25, D26, D27, D28, D29, D30, D31, diodebackward_2_out, diodebackward_6_out, diodebackward_9_out,
       diodebackward_11_out, F, Fout, I0, I1, IX, LD_t, LOAD, MUXOUT, nA, nand_1_out, nand_3_out, nand_5_out,
       nand_6_out, nand_8_out, nand_9_out, nand_10_out, nand_11_out, nand_12_out, nand_13_out, nand_14_out,
       nB, nCLRPC, nJMP, OR, pullup_1_out, pullup_4_out, pullup_5_out, Q4, Q5, RCO, SETC, ST, SUB, U3_pin9,
       U5_pin9, U6_pin9, U8_pin9, U9_pin9, U10_pin9, XOR, xor_1_out, xor_2_out, xor_3_out, xor_4_out;
  wire [3:0] _74161_1_pin11, U5_2_pin6, U5_2_pin13, U6_2_pin6, U6_2_pin10, U7_pin6, U7_pin13, U8_2_pin6;
  wire [3:1] U8_2_pin10;

  _74165 U5 (
    .pin1(LD), .pin2(GCLK), .pin3(D27), .pin4(D26), .pin5(D25), .pin6(D24), .pin8(1'b0), .pin9(U5_pin9),
    .pin10(1'b0), .pin11(D31), .pin12(D30), .pin13(D29), .pin14(D28), .pin15(1'b0), .pin16(1'b1));  // open: pin7
  Monoflop monoflop_1 (.C(LD), .R(1'b0), .Q(SETC), .nQ(RES));
  Monoflop monoflop_2 (.C(button_1_out), .R(1'b0), .Q(LD_t), .nQ(LD));
  Button button_1 (.out(button_1_out));
  _74138 U1 (
    .pin1(in_2), .pin2(in_3), .pin3(in_4), .pin4(1'b0), .pin5(1'b0), .pin6(1'b1), .pin7(nJMP), .pin8(1'b0),
    .pin9(ST), .pin10(SUB), .pin11(ADD), .pin12(XOR), .pin13(OR), .pin14(AND), .pin15(LOAD), .pin16(1'b1));
  _74165 U6 (
    .pin1(LD), .pin2(GCLK), .pin3(D19), .pin4(D18), .pin5(D17), .pin6(D16), .pin8(1'b0), .pin9(U6_pin9),
    .pin10(U5_pin9), .pin11(D23), .pin12(D22), .pin13(D21), .pin14(D20), .pin15(1'b0), .pin16(1'b1));  // open: pin7
  PullUp pullup_1 (.out(pullup_1_out));
  DiodeBackward diodebackward_1 (.in(LOAD), .out(pullup_1_out));
  DiodeBackward diodebackward_2 (.in(LOAD), .out(diodebackward_2_out));
  DiodeBackward diodebackward_3 (.in(ADD), .out(diodebackward_2_out));
  DiodeBackward diodebackward_4 (.in(SUB), .out(diodebackward_2_out));
  DiodeBackward diodebackward_5 (.in(nJMP), .out(diodebackward_2_out));
  PullUp pullup_2 (.out(diodebackward_2_out));
  DiodeBackward diodebackward_6 (.in(SUB), .out(diodebackward_6_out));
  DiodeBackward diodebackward_7 (.in(ST), .out(diodebackward_6_out));
  PullUp pullup_3 (.out(diodebackward_6_out));
  PullUp pullup_4 (.out(pullup_4_out));
  DiodeBackward diodebackward_8 (.in(SUB), .out(pullup_4_out));
  _74165 U3 (
    .pin1(LD), .pin2(GCLK), .pin3(D11), .pin4(D10), .pin5(D9), .pin6(D8), .pin8(1'b0), .pin9(U3_pin9),
    .pin10(U6_pin9), .pin11(D15), .pin12(D14), .pin13(D13), .pin14(D12), .pin15(1'b0), .pin16(1'b1));  // open: pin7
  PullUp pullup_5 (.out(pullup_5_out));
  DiodeBackward diodebackward_9 (.in(AND), .out(diodebackward_9_out));
  DiodeBackward diodebackward_10 (.in(OR), .out(diodebackward_9_out));
  PullUp pullup_6 (.out(diodebackward_9_out));
  DiodeBackward diodebackward_11 (.in(LOAD), .out(diodebackward_11_out));
  DiodeBackward diodebackward_12 (.in(OR), .out(diodebackward_11_out));
  DiodeBackward diodebackward_13 (.in(XOR), .out(diodebackward_11_out));
  DiodeBackward diodebackward_14 (.in(ADD), .out(diodebackward_11_out));
  DiodeBackward diodebackward_15 (.in(SUB), .out(diodebackward_11_out));
  DiodeBackward diodebackward_16 (.in(ST), .out(diodebackward_11_out));
  PullUp pullup_7 (.out(diodebackward_11_out));
  _74540 U2 (
    .pin1(1'b0), .pin2(diodebackward_11_out), .pin3(diodebackward_9_out), .pin4(pullup_5_out),
    .pin5(pullup_4_out), .pin6(diodebackward_6_out), .pin7(diodebackward_2_out), .pin8(pullup_1_out),
    .pin9(1'b0), .pin10(1'b0), .pin12(CLA), .pin13(F), .pin14(C), .pin15(nB), .pin16(nA), .pin17(I1),
    .pin18(I0), .pin19(1'b0), .pin20(1'b1));  // open: pin11
  _74165 U4 (
    .pin1(LD), .pin2(GCLK), .pin3(D3), .pin4(D2), .pin5(D1), .pin6(D0), .pin8(1'b0), .pin9(Bout),
    .pin10(U3_pin9), .pin11(D7), .pin12(D6), .pin13(D5), .pin14(D4), .pin15(1'b0), .pin16(1'b1));  // open: pin7
  _74161 _74161_1 (
    .pin1(RST), .pin2(clk), .pin3(1'b0), .pin4(1'b0), .pin5(1'b0), .pin6(1'b0), .pin7(1'b1), .pin8(1'b0),
    .pin9(1'b1), .pin10(1'b1), .pin11(_74161_1_pin11[3]), .pin12(_74161_1_pin11[2]),
    .pin13(_74161_1_pin11[1]), .pin14(_74161_1_pin11[0]), .pin15(_74161_1_pin15), .pin16(1'b1));
  _74161 _74161_2 (
    .pin1(RST), .pin2(clk), .pin3(1'b0), .pin4(1'b0), .pin5(1'b0), .pin6(1'b0), .pin7(1'b1), .pin8(1'b0),
    .pin9(1'b1), .pin10(_74161_1_pin15), .pin13(Q5), .pin14(Q4), .pin16(1'b1));  // open: pin11, pin12, pin15
  Seven_Seg_Hex seven_seg_hex_1 (.d(_74161_1_pin11), .dp(Q4));
  and and_1 (RCO, _74161_1_pin11[0], _74161_1_pin11[1], _74161_1_pin11[2], _74161_1_pin11[3], Q4);
  _74164 U5_2 (
    .pin1(1'b1), .pin2(Bout), .pin3(U5_2_pin6[3]), .pin4(U5_2_pin6[2]), .pin5(U5_2_pin6[1]),
    .pin6(U5_2_pin6[0]), .pin7(1'b0), .pin8(GCLK), .pin9(CLR), .pin10(U5_2_pin13[3]), .pin11(U5_2_pin13[2]),
    .pin12(U5_2_pin13[1]), .pin13(U5_2_pin13[0]), .pin14(1'b1));
  Monoflop monoflop_3 (.C(button_2_out), .R(1'b0), .nQ(nCLRPC));  // open: Q
  Button button_2 (.out(button_2_out));
  Seven_Seg_Hex seven_seg_hex_2 (.d(U5_2_pin6), .dp(1'b0));
  nand nand_1 (nand_1_out, clk, clk);
  nand nand_2 (RST, RES, nand_3_out);
  nand nand_3 (nand_3_out, RST, T0);
  Seven_Seg_Hex seven_seg_hex_3 (.d(U5_2_pin13), .dp(1'b0));
  _74153 _74153_1 (
    .pin1(1'b0), .pin2(in_4), .pin3(1'b0), .pin4(Fout), .pin5(SETC), .pin6(in_11), .pin7(MUXOUT),
    .pin8(1'b0), .pin10(1'b0), .pin11(1'b0), .pin12(1'b0), .pin13(1'b0), .pin14(A), .pin15(1'b1), .pin16(1'b1));  // open: pin9
  Seven_Seg_Hex seven_seg_hex_4 (.d(U6_2_pin6), .dp(1'b0));
  nand nand_4 (GCLK, nand_1_out, RST);
  Seven_Seg_Hex seven_seg_hex_5 (.d(U6_2_pin10), .dp(1'b0));
  Seven_Seg_Hex seven_seg_hex_6 (.d(U7_pin6), .dp(1'b0));
  _74164 U6_2 (
    .pin1(1'b1), .pin2(U5_2_pin13[0]), .pin3(U6_2_pin6[3]), .pin4(U6_2_pin6[2]), .pin5(U6_2_pin6[1]),
    .pin6(U6_2_pin6[0]), .pin7(1'b0), .pin8(GCLK), .pin9(CLR), .pin10(U6_2_pin10[3]), .pin11(U6_2_pin10[2]),
    .pin12(U6_2_pin10[1]), .pin13(U6_2_pin10[0]), .pin14(1'b1));
  Seven_Seg_Hex seven_seg_hex_7 (.d(U7_pin13), .dp(1'b0));
  _74595 U8 (
    .pin1(D30), .pin2(D29), .pin3(D28), .pin4(D27), .pin5(D26), .pin6(D25), .pin7(D24), .pin8(1'b0),
    .pin9(U8_pin9), .pin10(RES), .pin11(GCLK), .pin12(T0), .pin13(1'b0), .pin14(MUXOUT), .pin15(D31),
    .pin16(1'b1));
  xor xor_1 (xor_1_out, Aout, nA);
  xor xor_2 (xor_2_out, nB, Bout);
  nand nand_5 (nand_5_out, SETC, C);
  Seven_Seg_Hex seven_seg_hex_8 (.d(U8_2_pin6), .dp(1'b0));
  nand nand_6 (nand_6_out, C, C);
  Seven_Seg_Hex seven_seg_hex_9 (.d({U8_2_pin10, Aout}), .dp(1'b0));
  nand nand_7 (CLR, CLA, LD_t);
  nand nand_8 (nand_8_out, LD_t, nand_6_out);
  xor xor_3 (xor_3_out, xor_1_out, xor_2_out);
  _74164 U7 (
    .pin1(1'b1), .pin2(U6_2_pin10[0]), .pin3(U7_pin6[3]), .pin4(U7_pin6[2]), .pin5(U7_pin6[1]),
    .pin6(U7_pin6[0]), .pin7(1'b0), .pin8(GCLK), .pin9(CLR), .pin10(U7_pin13[3]), .pin11(U7_pin13[2]),
    .pin12(U7_pin13[1]), .pin13(U7_pin13[0]), .pin14(1'b1));
  _74595 U9 (
    .pin1(D22), .pin2(D21), .pin3(D20), .pin4(D19), .pin5(D18), .pin6(D17), .pin7(D16), .pin8(1'b0),
    .pin9(U9_pin9), .pin10(RES), .pin11(GCLK), .pin12(T0), .pin13(1'b0), .pin14(U8_pin9), .pin15(D23),
    .pin16(1'b1));
  xor xor_4 (xor_4_out, xor_3_out, Cin);
  nand nand_9 (nand_9_out, xor_3_out, Cin);
  nand nand_10 (nand_10_out, xor_1_out, xor_2_out);
  nand nand_11 (nand_11_out, nand_9_out, nand_10_out);
  _74164 U8_2 (
    .pin1(1'b1), .pin2(U7_pin13[0]), .pin3(U8_2_pin6[3]), .pin4(U8_2_pin6[2]), .pin5(U8_2_pin6[1]),
    .pin6(U8_2_pin6[0]), .pin7(1'b0), .pin8(GCLK), .pin9(CLR), .pin10(U8_2_pin10[3]), .pin11(U8_2_pin10[2]),
    .pin12(U8_2_pin10[1]), .pin13(Aout), .pin14(1'b1));
  nand nand_12 (nand_12_out, xor_4_out, I0);
  nand nand_13 (nand_13_out, I1, nand_11_out);
  nand nand_14 (nand_14_out, nand_11_out, F);
  _74595 U10 (
    .pin1(D14), .pin2(D13), .pin3(D12), .pin4(D11), .pin5(D10), .pin6(D9), .pin7(D8), .pin8(1'b0),
    .pin9(U10_pin9), .pin10(RES), .pin11(GCLK), .pin12(T0), .pin13(1'b0), .pin14(U9_pin9), .pin15(D15),
    .pin16(1'b1));
  nand nand_15 (Fout, nand_12_out, nand_13_out);
  nand nand_16 (Cout, nand_14_out, nand_14_out);
  Seven_Seg_Hex seven_seg_hex_10 (.d({D31, D30, D29, D28}), .dp(1'b0));
  Seven_Seg_Hex seven_seg_hex_11 (.d({D27, D26, D25, D24}), .dp(1'b0));
  Seven_Seg_Hex seven_seg_hex_12 (.d({D23, D22, D21, D20}), .dp(1'b0));
  _74595 U11 (
    .pin1(D6), .pin2(D5), .pin3(D4), .pin4(D3), .pin5(D2), .pin6(D1), .pin7(D0), .pin8(1'b0), .pin10(RES),
    .pin11(GCLK), .pin12(T0), .pin13(1'b0), .pin14(U10_pin9), .pin15(D7), .pin16(1'b1));  // open: pin9
  _7474 _7474_1 (
    .pin1(nand_8_out), .pin2(Cout), .pin3(GCLK), .pin4(nand_5_out), .pin5(Cin), .pin7(1'b0), .pin8(T0),
    .pin9(IX), .pin10(1'b1), .pin11(clk), .pin12(RCO), .pin13(1'b1), .pin14(1'b1));  // open: pin6
  Seven_Seg_Hex seven_seg_hex_13 (.d({D19, D18, D17, D16}), .dp(1'b0));
  Seven_Seg_Hex seven_seg_hex_14 (.d({D15, D14, D13, D12}), .dp(1'b0));
  Seven_Seg_Hex seven_seg_hex_15 (.d({D11, D10, D9, D8}), .dp(1'b0));
  Seven_Seg_Hex seven_seg_hex_16 (.d({D7, D6, D5, D4}), .dp(1'b0));
  Seven_Seg_Hex seven_seg_hex_17 (.d({D3, D2, D1, D0}), .dp(1'b0));

  // Other names for the same wires on the sheet: nCC = in_4; nLOAD = LD; nRES = RES

  // Notes on the sheet:
  //   clk: Hz: 2147483647
  //   Fibonacci 1
  //   Instruction Input
  //   Bit serial Fibonacci Generator
  //   STEP/RUN
  //   32 bit Shift Register B
  //   Instruction Decode
  //   CLA
  //   F
  //   ~B
  //   C
  //   ~A
  //   I1
  //   I0
  //   LOAD
  //   AND
  //   OR
  //   XOR
  //   ADD
  //   SUB
  //   STORE
  //   JMP
  //   Clock Sequencer
  //   # Clock
  //   (n-1)
  //   CLR PC
  //   32 bit Shift Register A
  //   ALU
  //   CLR ACC
  //   32 bit Shift Register C
  //   Carry is only set before Bit 0 of an operation
  //   Any residual carry is cleared before an operation
  //   Suppress Carry
  //   (n)
  //   Carry FF
endmodule
