// Digital circuit SPIDER_2024_9.dig as structural Verilog
module SPIDER_2024_9 (
  input  in_3,
  input  clk,
  input  in_5,
  input  nRD,
  input  nWR,
  input  in_8,
  input  in_9,
  input  in_10,
  input  in_11,
  input  ROM__gt_BUS,
  output GCLK,
  output T0,
  output nSS
);

  wire A0, A1, A2, A3, A4, A5, A6, A7, A8, A9, A10, A11, A12, A13, A14, A15, Ac0, Ac1, Ac2, Ac3, Ac4, Ac5,
       Ac6, Ac7, Ac8, Ac9, Ac10, Ac11, Ac12, Ac13, Ac14, Ac15, ADD, AND, Aout, Bout, BUS0, BUS1, BUS2, BUS3,
       BUS4, BUS5, BUS6, BUS7, BUS8, BUS9, BUS10, BUS11, BUS12, BUS13, BUS14, BUS15, button_1_out,
       button_2_out, button_3_out, button_4_out, button_5_out, button_6_out, button_7_out, button_8_out,
       button_9_out, button_10_out, button_11_out, button_12_out, button_13_out, button_14_out,
       button_15_out, button_16_out, button_17_out, button_18_out, C, Cin, CLA, CLR, Cout, D0, D1, D2, D3,
       D4, D5, D6, D7, d_ff_1_nq, d_ff_2_nq, d_ff_3_nq, d_ff_4_nq, d_ff_5_nq, d_ff_6_nq, d_ff_7_nq,
       d_ff_8_nq, d_ff_9_nq, d_ff_10_nq, d_ff_11_nq, d_ff_12_nq, diodebackward_1_out, diodebackward_3_out,
       diodebackward_9_out, F, Fout, I0, I1, IC17_2_nq, IC17_3_nq, IC17_4_nq, IC17_nq, IR0, IR1, IR2, IR3,
       IR4, IR5, IR6, IR7, LD, LOAD, MA0, MA1, MA2, MA3, MA4, MA5, MA6, MA7, MA8, MA9, MA10, MA11, MA12,
       MA13, MA14, MA15, nA, nand_3_out, nand_5_out, nand_6_out, nand_7_out, nand_8_out, nand_9_out,
       nand_10_out, nand_16_out, nand_17_out, nand_18_out, nand_19_out, nB, nCLRPC, nJMP, nLOAD, not_1_out,
       nROM__gt_BUS, nSE, OR, PC_Carry, PC_Cin, PCin, PCout, pullup_2_out, pullup_4_out, pullup_5_out,
       pullup_7_out, RCO, RES, ResC, ROM0, ROM1, ROM2, ROM3, ROM4, ROM5, ROM6, ROM7, ROM8, ROM9, ROM10,
       ROM11, ROM12, ROM13, ROM14, ROM15, RST, RUN, SETC, SetC_t, ST, SUB, U4_pin9, U6_pin9, U8_pin9,
       U10_pin9, U26_pin9, U27_pin9, XOR, xor_1_out, xor_2_out, xor_3_out, xor_4_out, xor_5_out, xor_6_out,
       ZERO, Zin;
  wire [3:0] d_ff_10_q, IC17_3_q, IC17_q, U12_pin11;
  wire [3:1] d_ff_4_q;

  _74165 U4 (
    .pin1(nLOAD), .pin2(GCLK), .pin3(BUS11), .pin4(BUS10), .pin5(BUS9), .pin6(BUS8), .pin8(1'b0),
    .pin9(U4_pin9), .pin10(1'b0), .pin11(BUS15), .pin12(BUS14), .pin13(BUS13), .pin14(BUS12), .pin15(1'b0),
    .pin16(1'b1));  // open: pin7
  _27C1024 U1 (
    .nCE(1'b0), .nOE(1'b0), .VPP(1'b1), .VDD(1'b1), .GND(1'b0), .I_O0(ROM0), .I_O1(ROM1), .I_O2(ROM2),
    .I_O3(ROM3), .I_O4(ROM4), .I_O5(ROM5), .I_O6(ROM6), .I_O7(ROM7), .A0(A0), .A1(A1), .A2(A2), .A3(A3),
    .A4(A4), .A5(A5), .A6(A6), .A7(A7), .A8(A8), .A9(A9), .A10(A10), .A11(A11), .A12(A12), .A13(A13),
    .A14(A14), .A15(A15), .I_O8(ROM8), .I_O9(ROM9), .I_O10(ROM10), .I_O11(ROM11), .I_O12(ROM12),
    .I_O13(ROM13), .I_O14(ROM14), .I_O15(ROM15), .VSS(1'b0));
  _74165 U5 (
    .pin1(nLOAD), .pin2(GCLK), .pin3(BUS3), .pin4(BUS2), .pin5(BUS1), .pin6(BUS0), .pin8(1'b0), .pin9(Bout),
    .pin10(U4_pin9), .pin11(BUS7), .pin12(BUS6), .pin13(BUS5), .pin14(BUS4), .pin15(1'b0), .pin16(1'b1));  // open: pin7
  DiodeForward diodeforward_1 (.in(BUS15), .out(Zin));
  DiodeForward diodeforward_2 (.in(BUS14), .out(Zin));
  DiodeForward diodeforward_3 (.in(BUS13), .out(Zin));
  DiodeForward diodeforward_4 (.in(BUS12), .out(Zin));
  DiodeForward diodeforward_5 (.in(BUS11), .out(Zin));
  DiodeForward diodeforward_6 (.in(BUS10), .out(Zin));
  DiodeForward diodeforward_7 (.in(BUS9), .out(Zin));
  DiodeForward diodeforward_8 (.in(BUS8), .out(Zin));
  DiodeForward diodeforward_9 (.in(BUS7), .out(Zin));
  DiodeForward diodeforward_10 (.in(BUS6), .out(Zin));
  DiodeForward diodeforward_11 (.in(BUS5), .out(Zin));
  DiodeForward diodeforward_12 (.in(BUS4), .out(Zin));
  DiodeForward diodeforward_13 (.in(BUS3), .out(Zin));
  DiodeForward diodeforward_14 (.in(BUS2), .out(Zin));
  DiodeForward diodeforward_15 (.in(BUS1), .out(Zin));
  DiodeForward diodeforward_16 (.in(BUS0), .out(Zin));
  PullDown pulldown_1 (.out(Zin));
  _74138 U2 (
    .pin1(in_8), .pin2(in_9), .pin3(in_10), .pin4(1'b0), .pin5(1'b0), .pin6(1'b1), .pin7(nJMP), .pin8(1'b0),
    .pin9(ST), .pin10(SUB), .pin11(ADD), .pin12(XOR), .pin13(OR), .pin14(AND), .pin15(LOAD), .pin16(1'b1));
  _62256 U22 (
    .A0(MA0), .A1(MA1), .A2(MA2), .A3(MA3), .A4(MA4), .A5(MA5), .A6(MA6), .A7(MA7), .A8(MA8), .A9(MA9),
    .A10(MA10), .A11(MA11), .A12(MA12), .nCE(1'b0), .nOE(nRD), .nWE(nWR), .D0(BUS8), .D1(BUS9), .D2(BUS10),
    .D3(BUS11), .D4(BUS12), .D5(BUS13), .D6(BUS14), .D7(BUS15), .VCC(1'b1), .GND(1'b0), .A13(MA13), .A14(MA14));
  _74595 U6 (
    .pin1(MA14), .pin2(MA13), .pin3(MA12), .pin4(MA11), .pin5(MA10), .pin6(MA9), .pin7(MA8), .pin8(1'b0),
    .pin9(U6_pin9), .pin10(nCLRPC), .pin11(GCLK), .pin12(nSS), .pin13(1'b0), .pin14(Fout), .pin15(MA15),
    .pin16(1'b1));
  DiodeBackward diodebackward_1 (.in(LOAD), .out(diodebackward_1_out));
  DiodeBackward diodebackward_2 (.in(nJMP), .out(diodebackward_1_out));
  PullUp pullup_1 (.out(diodebackward_1_out));
  DiodeBackward diodebackward_3 (.in(LOAD), .out(diodebackward_3_out));
  DiodeBackward diodebackward_4 (.in(ADD), .out(diodebackward_3_out));
  DiodeBackward diodebackward_5 (.in(SUB), .out(diodebackward_3_out));
  DiodeBackward diodebackward_6 (.in(nJMP), .out(diodebackward_3_out));
  PullUp pullup_2 (.out(pullup_2_out));
  PullUp pullup_3 (.out(diodebackward_3_out));
  DiodeBackward diodebackward_7 (.in(SUB), .out(pullup_2_out));
  PullUp pullup_4 (.out(pullup_4_out));
  DiodeBackward diodebackward_8 (.in(SUB), .out(pullup_4_out));
  _74595 U7 (
    .pin1(MA6), .pin2(MA5), .pin3(MA4), .pin4(MA3), .pin5(MA2), .pin6(MA1), .pin7(MA0), .pin8(1'b0),
    .pin10(nCLRPC), .pin11(GCLK), .pin12(nSS), .pin13(1'b0), .pin14(U6_pin9), .pin15(MA7), .pin16(1'b1));  // open: pin9
  PullUp pullup_5 (.out(pullup_5_out));
  DiodeBackward diodebackward_9 (.in(AND), .out(diodebackward_9_out));
  DiodeBackward diodebackward_10 (.in(OR), .out(diodebackward_9_out));
  PullUp pullup_6 (.out(diodebackward_9_out));
  PullUp pullup_7 (.out(pullup_7_out));
  DiodeBackward diodebackward_11 (.in(LOAD), .out(pullup_7_out));
  DiodeBackward diodebackward_12 (.in(OR), .out(pullup_7_out));
  DiodeBackward diodebackward_13 (.in(XOR), .out(pullup_7_out));
  DiodeBackward diodebackward_14 (.in(ADD), .out(pullup_7_out));
  DiodeBackward diodebackward_15 (.in(SUB), .out(pullup_7_out));
  DiodeBackward diodebackward_16 (.in(ST), .out(pullup_7_out));
  DiodeBackward diodebackward_17 (.in(nJMP), .out(pullup_7_out));
  _62256 U23 (
    .A0(MA0), .A1(MA1), .A2(MA2), .A3(MA3), .A4(MA4), .A5(MA5), .A6(MA6), .A7(MA7), .A8(MA8), .A9(MA9),
    .A10(MA10), .A11(MA11), .A12(MA12), .nCE(1'b0), .nOE(nRD), .nWE(nWR), .D0(BUS0), .D1(BUS1), .D2(BUS2),
    .D3(BUS3), .D4(BUS4), .D5(BUS5), .D6(BUS6), .D7(BUS7), .VCC(1'b1), .GND(1'b0), .A13(MA13), .A14(MA14));
  _74540 U3 (
    .pin1(1'b0), .pin2(pullup_7_out), .pin3(diodebackward_9_out), .pin4(pullup_5_out), .pin5(pullup_4_out),
    .pin6(pullup_2_out), .pin7(diodebackward_3_out), .pin8(diodebackward_1_out), .pin9(Zin), .pin10(1'b0),
    .pin11(ZERO), .pin12(CLA), .pin13(F), .pin14(C), .pin15(nB), .pin16(nA), .pin17(I1), .pin18(I0),
    .pin19(1'b0), .pin20(1'b1));
  _74595 U8 (
    .pin1(A14), .pin2(A13), .pin3(A12), .pin4(A11), .pin5(A10), .pin6(A9), .pin7(A8), .pin8(1'b0),
    .pin9(U8_pin9), .pin10(nCLRPC), .pin11(GCLK), .pin12(T0), .pin13(1'b0), .pin14(PCin), .pin15(A15),
    .pin16(1'b1));
  _74161 U12 (
    .pin1(RST), .pin2(clk), .pin3(1'b0), .pin4(1'b0), .pin5(1'b0), .pin6(1'b0), .pin7(1'b1), .pin8(1'b0),
    .pin9(1'b1), .pin10(1'b1), .pin11(U12_pin11[3]), .pin12(U12_pin11[2]), .pin13(U12_pin11[1]),
    .pin14(U12_pin11[0]), .pin15(RCO), .pin16(1'b1));
  xor xor_1 (xor_1_out, Aout, nA);
  xor xor_2 (xor_2_out, nB, Bout);
  nand nand_1 (SetC_t, SETC, C);
  nand nand_2 (CLR, CLA, LD);
  Seven_Seg_Hex seven_seg_hex_1 (.d({A15, A14, A13, A12}), .dp(1'b0));
  nand nand_3 (nand_3_out, C, C);
  Seven_Seg_Hex seven_seg_hex_2 (.d({A11, A9, A10, A8}), .dp(1'b0));
  nand nand_4 (ResC, nand_3_out, LD);
  _74595 U9 (
    .pin1(A6), .pin2(A5), .pin3(A4), .pin4(A3), .pin5(A2), .pin6(A1), .pin7(A0), .pin8(1'b0), .pin9(PCout),
    .pin10(nCLRPC), .pin11(GCLK), .pin12(T0), .pin13(1'b0), .pin14(U8_pin9), .pin15(A7), .pin16(1'b1));
  Seven_Seg_Hex seven_seg_hex_3 (.d({A7, A6, A5, A4}), .dp(1'b0));
  Seven_Seg_Hex seven_seg_hex_4 (.d(U12_pin11), .dp(1'b0));
  xor xor_3 (xor_3_out, xor_1_out, xor_2_out);
  Seven_Seg_Hex seven_seg_hex_5 (.d({A3, A2, A1, A0}), .dp(1'b0));
  xor xor_4 (xor_4_out, xor_3_out, Cin);
  nand nand_5 (nand_5_out, xor_3_out, Cin);
  nand nand_6 (nand_6_out, xor_1_out, xor_2_out);
  Seven_Seg_Hex seven_seg_hex_6 (.d({BUS15, BUS14, BUS13, BUS12}), .dp(1'b0));
  _7474 U13 (
    .pin1(1'b1), .pin2(RCO), .pin3(clk), .pin4(1'b1), .pin5(RUN), .pin6(T0), .pin7(1'b0), .pin9(PC_Cin),
    .pin10(nLOAD), .pin11(GCLK), .pin12(PC_Carry), .pin13(1'b1), .pin14(1'b1));  // open: pin8
  nand nand_7 (nand_7_out, nand_5_out, nand_6_out);
  Seven_Seg_Hex seven_seg_hex_7 (.d({BUS11, BUS10, BUS9, BUS8}), .dp(1'b0));
  _74595 U10 (
    .pin1(Ac14), .pin2(Ac13), .pin3(Ac12), .pin4(Ac11), .pin5(Ac10), .pin6(Ac9), .pin7(Ac8), .pin8(1'b0),
    .pin9(U10_pin9), .pin10(nCLRPC), .pin11(GCLK), .pin12(T0), .pin13(1'b0), .pin14(Fout), .pin15(Ac15),
    .pin16(1'b1));
  Seven_Seg_Hex seven_seg_hex_8 (.d({BUS7, BUS6, BUS5, BUS4}), .dp(1'b0));
  Seven_Seg_Hex seven_seg_hex_9 (.d({BUS3, BUS2, BUS1, BUS0}), .dp(1'b0));
  nand nand_8 (nand_8_out, xor_4_out, I0);
  nand nand_9 (nand_9_out, I1, nand_7_out);
  nand nand_10 (nand_10_out, nand_7_out, F);
  Seven_Seg_Hex seven_seg_hex_10 (.d({Ac15, Ac14, Ac13, Ac12}), .dp(1'b0));
  not not_1 (not_1_out, clk);
  nand nand_11 (Fout, nand_8_out, nand_9_out);
  nand nand_12 (Cout, nand_10_out, nand_10_out);
  Seven_Seg_Hex seven_seg_hex_11 (.d({Ac11, Ac10, Ac9, Ac8}), .dp(1'b0));
  nand nand_13 (GCLK, not_1_out, RST);
  nand nand_14 (RST, RES, nSE);
  nand nand_15 (nSE, RST, T0);
  nand nand_16 (nand_16_out, nSE, T0);
  _74595 U11 (
    .pin1(Ac6), .pin2(Ac5), .pin3(Ac4), .pin4(Ac3), .pin5(Ac2), .pin6(Ac1), .pin7(Ac0), .pin8(1'b0),
    .pin9(Aout), .pin10(nCLRPC), .pin11(GCLK), .pin12(T0), .pin13(1'b0), .pin14(U10_pin9), .pin15(Ac7),
    .pin16(1'b1));
  Seven_Seg_Hex seven_seg_hex_12 (.d({Ac7, Ac6, Ac4, Ac5}), .dp(1'b0));
  Seven_Seg_Hex seven_seg_hex_13 (.d({Ac3, Ac2, Ac1, Ac0}), .dp(1'b0));
  not not_2 (nSS, nand_16_out);
  _7474 U21 (
    .pin1(ResC), .pin2(Cout), .pin3(GCLK), .pin4(SetC_t), .pin5(Cin), .pin7(1'b0), .pin10(1'b1),
    .pin11(1'b1), .pin12(1'b1), .pin13(1'b1), .pin14(1'b1));  // open: pin6, pin8, pin9
  Seven_Seg_Hex seven_seg_hex_14 (.d({IR7, IR6, IR5, IR4}), .dp(1'b0));
  LED led_1 (.in(Cin));
  Seven_Seg_Hex seven_seg_hex_15 (.d({IR3, IR2, IR1, IR0}), .dp(1'b0));
  _74595 U26 (
    .pin1(BUS14), .pin2(BUS13), .pin3(BUS12), .pin4(BUS11), .pin5(BUS10), .pin6(BUS9), .pin7(BUS8),
    .pin8(1'b0), .pin9(U26_pin9), .pin10(nCLRPC), .pin11(GCLK), .pin12(T0), .pin13(1'b0), .pin14(Fout),
    .pin15(BUS15), .pin16(1'b1));
  Seven_Seg_Hex seven_seg_hex_16 (.d({D7, D6, D5, D4}), .dp(1'b0));
  xor xor_5 (xor_5_out, PCout, PC_Cin);
  nand nand_17 (nand_17_out, PCout, PC_Cin);
  Seven_Seg_Hex seven_seg_hex_17 (.d({D3, D2, D1, D0}), .dp(1'b0));
  assign BUS15 = ~in_11 ? IC17_q[3] : 1'bz;  // DriverInvSel driverinvsel_1
  LED led_2 (.in(IC17_q[3]));
  D_FF IC17 (.D(IC17_nq), .C(button_1_out), .Q(IC17_q[3]), .nQ(IC17_nq));
  Button button_1 (.out(button_1_out));
  assign BUS14 = ~in_11 ? IC17_q[2] : 1'bz;  // DriverInvSel driverinvsel_2
  LED led_3 (.in(IC17_q[2]));
  D_FF d_ff_1 (.D(d_ff_1_nq), .C(button_2_out), .Q(IC17_q[2]), .nQ(d_ff_1_nq));
  Button button_2 (.out(button_2_out));
  Seven_Seg_Hex seven_seg_hex_18 (.d({MA15, MA14, MA13, MA12}), .dp(1'b0));
  xor xor_6 (xor_6_out, nJMP, 1'b1);
  xor xor_7 (PC_Carry, 1'b1, nand_17_out);
  assign BUS13 = ~in_11 ? IC17_q[1] : 1'bz;  // DriverInvSel driverinvsel_3
  LED led_4 (.in(IC17_q[1]));
  D_FF d_ff_2 (.D(d_ff_2_nq), .C(button_3_out), .Q(IC17_q[1]), .nQ(d_ff_2_nq));
  Button button_3 (.out(button_3_out));
  Seven_Seg_Hex seven_seg_hex_19 (.d({MA11, MA10, MA9, MA8}), .dp(1'b0));
  assign BUS12 = ~in_11 ? IC17_q[0] : 1'bz;  // DriverInvSel driverinvsel_4
  LED led_5 (.in(IC17_q[0]));
  D_FF d_ff_3 (.D(d_ff_3_nq), .C(button_4_out), .Q(IC17_q[0]), .nQ(d_ff_3_nq));
  Button button_4 (.out(button_4_out));
  _74595 U27 (
    .pin1(BUS6), .pin2(BUS5), .pin3(BUS4), .pin4(BUS3), .pin5(BUS2), .pin6(BUS1), .pin7(BUS0), .pin8(1'b0),
    .pin9(U27_pin9), .pin10(nCLRPC), .pin11(GCLK), .pin12(T0), .pin13(1'b0), .pin14(U26_pin9), .pin15(BUS7),
    .pin16(1'b1));
  Seven_Seg_Hex seven_seg_hex_20 (.d({MA7, MA6, MA5, MA4}), .dp(1'b0));
  nand nand_18 (nand_18_out, xor_5_out, nJMP);
  nand nand_19 (nand_19_out, xor_6_out, in_3);
  assign BUS11 = ~in_11 ? d_ff_4_q[3] : 1'bz;  // DriverInvSel driverinvsel_5
  LED led_6 (.in(d_ff_4_q[3]));
  D_FF d_ff_4 (.D(d_ff_4_nq), .C(button_5_out), .Q(d_ff_4_q[3]), .nQ(d_ff_4_nq));
  Button button_5 (.out(button_5_out));
  Seven_Seg_Hex seven_seg_hex_21 (.d({MA3, MA2, MA1, MA0}), .dp(1'b0));
  xor xor_8 (PCin, nand_18_out, nand_19_out);
  assign BUS10 = ~in_11 ? d_ff_4_q[2] : 1'bz;  // DriverInvSel driverinvsel_6
  LED led_7 (.in(d_ff_4_q[2]));
  D_FF d_ff_5 (.D(d_ff_5_nq), .C(button_6_out), .Q(d_ff_4_q[2]), .nQ(d_ff_5_nq));
  Button button_6 (.out(button_6_out));
  assign BUS9 = ~in_11 ? d_ff_4_q[1] : 1'bz;  // DriverInvSel driverinvsel_7
  LED led_8 (.in(d_ff_4_q[1]));
  D_FF d_ff_6 (.D(d_ff_6_nq), .C(button_7_out), .Q(d_ff_4_q[1]), .nQ(d_ff_6_nq));
  Button button_7 (.out(button_7_out));
  assign BUS8 = ~in_11 ? d_ff_4_q[1] : 1'bz;  // DriverInvSel driverinvsel_8
  LED led_9 (.in(d_ff_4_q[1]));
  D_FF IC17_2 (.D(IC17_2_nq), .C(button_8_out), .Q(d_ff_4_q[1]), .nQ(IC17_2_nq));
  Button button_8 (.out(button_8_out));
  Seven_Seg_Hex seven_seg_hex_22 (.d(IC17_q), .dp(1'b0));
  Seven_Seg_Hex seven_seg_hex_23 (.d({d_ff_4_q, d_ff_4_q[1]}), .dp(1'b0));
  LED led_10 (.in(IC17_3_q[3]));
  D_FF IC17_3 (.D(IC17_3_nq), .C(button_9_out), .Q(IC17_3_q[3]), .nQ(IC17_3_nq));
  _74541 _74541_1 (
    .pin1(nROM__gt_BUS), .pin2(ROM0), .pin3(ROM1), .pin4(ROM2), .pin5(ROM3), .pin6(ROM4), .pin7(ROM5),
    .pin8(ROM6), .pin9(ROM7), .pin10(1'b0), .pin11(BUS7), .pin12(BUS6), .pin13(BUS5), .pin14(BUS4),
    .pin15(BUS3), .pin16(BUS2), .pin17(BUS1), .pin18(BUS0), .pin19(nROM__gt_BUS), .pin20(1'b1));
  _74541 _74541_2 (
    .pin1(nROM__gt_BUS), .pin2(ROM8), .pin3(ROM9), .pin4(ROM10), .pin5(ROM11), .pin6(ROM12), .pin7(ROM13),
    .pin8(ROM14), .pin9(ROM15), .pin10(1'b0), .pin11(BUS15), .pin12(BUS14), .pin13(BUS13), .pin14(BUS12),
    .pin15(BUS11), .pin16(BUS10), .pin17(BUS9), .pin18(BUS8), .pin19(nROM__gt_BUS), .pin20(1'b1));
  assign BUS7 = ~in_11 ? IC17_3_q[3] : 1'bz;  // DriverInvSel driverinvsel_9
  LED led_11 (.in(IC17_3_q[2]));
  D_FF d_ff_7 (.D(d_ff_7_nq), .C(button_10_out), .Q(IC17_3_q[2]), .nQ(d_ff_7_nq));
  Button button_9 (.out(button_9_out));
  assign BUS6 = ~in_11 ? IC17_3_q[2] : 1'bz;  // DriverInvSel driverinvsel_10
  LED led_12 (.in(IC17_3_q[1]));
  D_FF d_ff_8 (.D(d_ff_8_nq), .C(button_11_out), .Q(IC17_3_q[1]), .nQ(d_ff_8_nq));
  Button button_10 (.out(button_10_out));
  assign BUS5 = ~in_11 ? IC17_3_q[1] : 1'bz;  // DriverInvSel driverinvsel_11
  LED led_13 (.in(IC17_3_q[0]));
  D_FF d_ff_9 (.D(d_ff_9_nq), .C(button_12_out), .Q(IC17_3_q[0]), .nQ(d_ff_9_nq));
  Button button_11 (.out(button_11_out));
  assign BUS4 = ~in_11 ? IC17_3_q[0] : 1'bz;  // DriverInvSel driverinvsel_12
  LED led_14 (.in(d_ff_10_q[3]));
  D_FF d_ff_10 (.D(d_ff_10_nq), .C(button_13_out), .Q(d_ff_10_q[3]), .nQ(d_ff_10_nq));
  Button button_12 (.out(button_12_out));
  assign BUS3 = ~in_11 ? d_ff_10_q[3] : 1'bz;  // DriverInvSel driverinvsel_13
  LED led_15 (.in(d_ff_10_q[2]));
  D_FF d_ff_11 (.D(d_ff_11_nq), .C(button_14_out), .Q(d_ff_10_q[2]), .nQ(d_ff_11_nq));
  Button button_13 (.out(button_13_out));
  assign BUS2 = ~in_11 ? d_ff_10_q[2] : 1'bz;  // DriverInvSel driverinvsel_14
  LED led_16 (.in(d_ff_10_q[1]));
  D_FF d_ff_12 (.D(d_ff_12_nq), .C(button_15_out), .Q(d_ff_10_q[1]), .nQ(d_ff_12_nq));
  Button button_14 (.out(button_14_out));
  assign BUS1 = ~in_11 ? d_ff_10_q[1] : 1'bz;  // DriverInvSel driverinvsel_15
  LED led_17 (.in(d_ff_10_q[0]));
  D_FF IC17_4 (.D(IC17_4_nq), .C(button_16_out), .Q(d_ff_10_q[0]), .nQ(IC17_4_nq));
  Button button_15 (.out(button_15_out));
  assign BUS0 = ~in_11 ? d_ff_10_q[0] : 1'bz;  // DriverInvSel driverinvsel_16
  Button button_16 (.out(button_16_out));
  LED led_18 (.in(Zin));
  LED led_19 (.in(RUN));
  Seven_Seg_Hex seven_seg_hex_24 (.d(IC17_3_q), .dp(1'b0));
  Seven_Seg_Hex seven_seg_hex_25 (.d(d_ff_10_q), .dp(1'b0));
  Monoflop monoflop_1 (.C(button_17_out), .R(1'b0), .Q(LD), .nQ(nLOAD));
  Button button_17 (.out(button_17_out));
  Monoflop monoflop_2 (.C(nLOAD), .R(1'b0), .Q(SETC), .nQ(RES));
  Monoflop monoflop_3 (.C(button_18_out), .R(1'b0), .nQ(nCLRPC));  // open: Q
  Button button_18 (.out(button_18_out));

  // Other names for the same wires on the sheet: nCE = in_5; nLD_INC = nJMP; nOE = nRD; nRRES = nCLRPC; nWE = nWR;
  //   R0 = D0; R1 = D1; R2 = D2; R3 = D3; R4 = D4; R5 = D5; R6 = D6; R7 = D7; R8 = IR0; R9 = IR1; R10 = IR2;
  //   R11 = IR3; R12 = IR4; R13 = IR5; R14 = IR6; R15 = IR7; Rout = in_3; SCLK = GCLK

  // Notes on the sheet:
  //   clk: Hz: 20
  //   nRD: default 1
  //   nWR: default 1
  //   in_11: default 1
  //   ROM__gt_BUS: default 1
  //   Spider 16-bit Serial CPU
  //   BUS REGISTER B
  //   Instruction ROM
  //   ZERO
  //   Instruction Input
  //   MEMORY  ADDRESS REGISTER
  //   RAM HI
  //   Instruction Decode
  //   CLA
  //   C
  //   F
  //   ~B
  //   ~A
  //   I0
  //   I1
  //   RAM LO
  //   LOAD
  //   AND
  //   OR
  //   XOR
  //   ADD
  //   SUB
  //   STORE
  //   JMP
  //   PROGRAM COUNTER
  //   Clock Sequencer 3 packages
  //   ALU
  //   CLR ACC
  //   U20A
  //   U20B
  //   U19A
  //   U19D
  //   U19B
  //   U19C
  //   Clock #
  //   U20C
  //   U20D
  //   U17A
  //   U17B
  //   Carry is only set before Bit 0 of an operation
  //   Any residual carry is cleared before an operation
  //   Carry FF
  //   U17C
  //   DATA BUS
  //   U17D
  //   U18B
  //   U18A
  //   Suppress Carry
  //   ACCUMULATOR
  //   U24A
  //   U18C
  //   U18D
  //   U14B
  //   U14C
  //   U14D
  //   U14A
  //   U15B
  //   INSTRUCTION
  //   XOR Program Counter (Incrementer)  2 packages
  //   CARRY
  //   U15A
  //   U16A
  //   DATA
  //   MEMORY  WRITE REGISTER
  //   RAM ADDRESS
  //   U15C
  //   ENTER H
  //   U16C
  //   U16B
  //   U15D
  //   Data Input
  //   ROM->BUS
  //   ENTER L
  //   CLR PC
endmodule
