// Digital circuit SPIder_2024_5.dig as structural Verilog
module SPIder_2024_5 (
  input  clk,
  input  in_4,
  input  in_5,
  input  in_6,
  input  A,
  input  B,
  input  C,
  input  in_10,
  input  in_11,
  input  in_12,
  input  AC,
  input  BC,
  input  CC,
  input  DC,
  input  in_18,
  input  nCE,
  input  nRD,
  input  nWR,
  input  in_22,
  input  in_23,
  input  in_24,
  input  in_25,
  input  in_26,
  input  nSWITCH_RAM,
  input  in_28,
  input  in_29,
  input  in_30,
  input  in_31,
  input  in_32,
  output GCLK,
  output T0,
  output Kout
);

  wire _0_out, _1_out, _2_out, _3_out, _4_out, _5_out, _6_out, _7_out, _8_out, _9_out, _74138_1_pin7,
       _74138_1_pin9, _74138_1_pin10, _74138_1_pin11, _74138_1_pin12, _74138_1_pin13, _74138_1_pin14,
       _74138_1_pin15, _74139_2_pin4, _74139_2_pin5, _74139_2_pin6, _74139_2_pin7, _74157_1_pin7,
       _74157_1_pin9, _74157_1_pin12, _74173_4_pin11, _74173_4_pin12, _74173_4_pin13, _74173_4_pin14,
       _74540_1_pin11, _74540_1_pin12, _74540_1_pin13, _74540_1_pin14, _74540_1_pin15, _74540_1_pin16,
       _74540_1_pin17, A0, A1, A2, A3, A4, A5, A6, A7, A8, A9, A10, A11, A12, A13, A14, A15, A_out, Ac0, Ac1,
       Ac2, Ac3, Ac4, Ac5, Ac6, Ac7, Ac8, Ac9, Ac10, Ac11, Ac12, Ac13, Ac14, Ac15, ADD, Address_out, ALU,
       ALU_to_RAM_out, AND, B_out, Bout, BUS0, BUS1, BUS2, BUS3, BUS4, BUS5, BUS6, BUS7, BUS8, BUS9, BUS10,
       BUS11, BUS12, BUS13, BUS14, BUS15, button_1_out, button_2_out, C_out, C_t, Cin, CLA, Clear_out, CLR,
       Cout, D0, D1, D2, D3, D4, D5, D6, D7, D_out, Dec_out, Deposit_nWR_out, diodebackward_1_out,
       diodebackward_3_out, diodebackward_8_out, diodebackward_12_out, diodebackward_15_out,
       diodebackward_30_out, diodebackward_63_out, diodebackward_68_out, diodebackward_70_out,
       diodebackward_72_out, diodeforward_17_out, DN, E_out, Examine_nRD_out, F, F_out, Fout, GO, I0, I1,
       Inc_out, IR0, IR1, IR2, IR3, IR4, IR5, IR6, IR7, IX, LD, LOAD, MA0, MA1, MA2, MA3, MA4, MA5, MA6, MA7,
       MA8, MA9, MA10, MA11, MA12, MA13, MA14, MA15, MADout, nA, nALB, nand_3_out, nand_5_out, nand_9_out,
       nand_11_out, nand_12_out, nand_13_out, nand_14_out, nand_15_out, nand_16_out, nand_17_out,
       nand_18_out, nand_19_out, nB, nCLRPC, nDE, nJMP, nLATCH, nLD, nLOAD, not_9_out, not_10_out, nRD_t,
       nWR_t, OR, PC_Carry, PC_Cin, PC_plus_1, PCin, PCout, pullup_2_out, pullup_3_out, pullup_6_out,
       pullup_7_out, pullup_9_out, pullup_12_out, pullup_13_out, pullup_14_out, pullup_17_out, pullup_18_out,
       RAMout, RCO, RES, ResC, RST, RUN, S0, S1, S2, S3, S4, S5, S6, S7, S8, S9, S10, S11, S12, S13, S14,
       S15, SETC, SetC_t, ST, SUB, U8_pin9, U17_pin9, U19_2_pin9, U19_3_pin9, U20_4_pin9, U27_pin9, UP, XOR,
       xor_1_out, xor_2_out, xor_3_out, xor_4_out, ZERO, Zin;
  wire [3:0] U20_pin11;

  DiodeBackward diodebackward_1 (.in(Address_out), .out(diodebackward_1_out));
  PullUp pullup_1 (.out(diodebackward_1_out));
  PullUp pullup_2 (.out(pullup_2_out));
  DiodeBackward diodebackward_2 (.in(Dec_out), .out(pullup_2_out));
  not not_1 (nLOAD, _74540_1_pin11);
  PullUp pullup_3 (.out(pullup_3_out));
  DiodeBackward diodebackward_3 (.in(ALU_to_RAM_out), .out(diodebackward_3_out));
  DiodeBackward diodebackward_4 (.in(Examine_nRD_out), .out(diodebackward_3_out));
  DiodeBackward diodebackward_5 (.in(Dec_out), .out(diodebackward_3_out));
  DiodeBackward diodebackward_6 (.in(Inc_out), .out(pullup_3_out));
  DiodeBackward diodebackward_7 (.in(Inc_out), .out(diodebackward_3_out));
  PullUp pullup_4 (.out(diodebackward_3_out));
  DiodeBackward diodebackward_8 (.in(Examine_nRD_out), .out(diodebackward_8_out));
  DiodeBackward diodebackward_9 (.in(Deposit_nWR_out), .out(diodebackward_8_out));
  not not_2 (ALU, _74540_1_pin15);
  PullUp pullup_5 (.out(diodebackward_8_out));
  PullUp pullup_6 (.out(pullup_6_out));
  DiodeBackward diodebackward_10 (.in(ALU_to_RAM_out), .out(pullup_6_out));
  DiodeBackward diodebackward_11 (.in(Deposit_nWR_out), .out(pullup_6_out));
  not not_3 (nRD_t, _74540_1_pin17);
  not not_4 (nWR_t, _74540_1_pin16);
  nand nand_1 (UP, _74540_1_pin13, _74540_1_pin14);
  nand nand_2 (DN, _74540_1_pin12, _74540_1_pin14);
  PullUp pullup_7 (.out(pullup_7_out));
  DiodeBackward diodebackward_12 (.in(Clear_out), .out(diodebackward_12_out));
  DiodeBackward diodebackward_13 (.in(Examine_nRD_out), .out(pullup_7_out));
  _74173 _74173_1 (
    .pin1(1'b0), .pin2(1'b0), .pin3(S12), .pin4(S13), .pin5(S14), .pin6(S15), .pin7(nLATCH), .pin8(1'b0),
    .pin9(1'b0), .pin10(1'b0), .pin11(S11), .pin12(S10), .pin13(S9), .pin14(S8), .pin15(RES), .pin16(1'b1));
  _74139 _74139_1 (
    .pin1(1'b1), .pin2(1'b1), .pin3(1'b1), .pin8(1'b0), .pin11(nALB), .pin12(nDE), .pin13(1'b0), .pin14(ALU),
    .pin15(in_10), .pin16(1'b1));  // open: pin4, pin5, pin6, pin7, pin9, pin10
  PullUp pullup_8 (.out(diodebackward_12_out));
  Button #(.activeLow("true")) ALU_to_RAM (.out(ALU_to_RAM_out));
  Button #(.activeLow("true")) Clear (.out(Clear_out));
  Button #(.activeLow("true")) Examine_nRD (.out(Examine_nRD_out));
  Button #(.activeLow("true")) Deposit_nWR (.out(Deposit_nWR_out));
  Button #(.activeLow("true")) Dec (.out(Dec_out));
  Button #(.activeLow("true")) Inc (.out(Inc_out));
  Button #(.activeLow("true")) Address (.out(Address_out));
  _74540 _74540_1 (
    .pin1(1'b0), .pin2(diodebackward_12_out), .pin3(pullup_7_out), .pin4(pullup_6_out),
    .pin5(diodebackward_8_out), .pin6(diodebackward_3_out), .pin7(pullup_3_out), .pin8(pullup_2_out),
    .pin9(diodebackward_1_out), .pin10(1'b0), .pin11(_74540_1_pin11), .pin12(_74540_1_pin12),
    .pin13(_74540_1_pin13), .pin14(_74540_1_pin14), .pin15(_74540_1_pin15), .pin16(_74540_1_pin16),
    .pin17(_74540_1_pin17), .pin18(RES), .pin19(1'b0), .pin20(1'b1));
  _74165 U27 (
    .pin1(nLD), .pin2(GCLK), .pin3(S11), .pin4(S10), .pin5(S9), .pin6(S8), .pin8(1'b0), .pin9(U27_pin9),
    .pin10(1'b0), .pin11(S15), .pin12(S14), .pin13(S13), .pin14(S12), .pin15(1'b0), .pin16(1'b1));  // open: pin7
  _74173 _74173_2 (
    .pin1(1'b0), .pin2(1'b0), .pin3(S8), .pin4(S9), .pin5(S10), .pin6(S11), .pin7(nLATCH), .pin8(1'b0),
    .pin9(1'b0), .pin10(1'b0), .pin11(S7), .pin12(S6), .pin13(S5), .pin14(S4), .pin15(RES), .pin16(1'b1));
  Button #(.activeLow("true")) u_C (.out(C_out));
  Button #(.activeLow("true")) _8 (.out(_8_out));
  Button #(.activeLow("true")) _4 (.out(_4_out));
  Button #(.activeLow("true")) _0 (.out(_0_out));
  Seven_Seg_Hex seven_seg_hex_1 (.d({S15, S14, S13, S12}), .dp(1'b0));
  Seven_Seg_Hex seven_seg_hex_2 (.d({S11, S10, S9, S8}), .dp(1'b0));
  Button #(.activeLow("true")) D (.out(D_out));
  Button #(.activeLow("true")) _9 (.out(_9_out));
  Button #(.activeLow("true")) _5 (.out(_5_out));
  Button #(.activeLow("true")) _1 (.out(_1_out));
  _74165 U28 (
    .pin1(nLD), .pin2(GCLK), .pin3(S3), .pin4(S2), .pin5(S1), .pin6(S0), .pin8(1'b0), .pin9(Kout),
    .pin10(U27_pin9), .pin11(S7), .pin12(S6), .pin13(S5), .pin14(S4), .pin15(1'b0), .pin16(1'b1));  // open: pin7
  Seven_Seg_Hex seven_seg_hex_3 (.d({S7, S6, S5, S4}), .dp(1'b0));
  _74173 _74173_3 (
    .pin1(1'b0), .pin2(1'b0), .pin3(S4), .pin4(S5), .pin5(S6), .pin6(S7), .pin7(nLATCH), .pin8(1'b0),
    .pin9(1'b0), .pin10(1'b0), .pin11(S3), .pin12(S2), .pin13(S1), .pin14(S0), .pin15(RES), .pin16(1'b1));
  Seven_Seg_Hex seven_seg_hex_4 (.d({S3, S2, S1, S0}), .dp(1'b0));
  Button #(.activeLow("true")) E (.out(E_out));
  Button #(.activeLow("true")) u_A (.out(A_out));
  Button #(.activeLow("true")) _6 (.out(_6_out));
  Button #(.activeLow("true")) _2 (.out(_2_out));
  Button #(.activeLow("true")) u_F (.out(F_out));
  Button #(.activeLow("true")) u_B (.out(B_out));
  Button #(.activeLow("true")) _7 (.out(_7_out));
  Button #(.activeLow("true")) _3 (.out(_3_out));
  _74173 _74173_4 (
    .pin1(1'b0), .pin2(1'b0), .pin3(S0), .pin4(S1), .pin5(S2), .pin6(S3), .pin7(nLATCH), .pin8(1'b0),
    .pin9(1'b0), .pin10(1'b0), .pin11(_74173_4_pin11), .pin12(_74173_4_pin12), .pin13(_74173_4_pin13),
    .pin14(_74173_4_pin14), .pin15(RES), .pin16(1'b1));
  _74138 _74138_1 (
    .pin1(A), .pin2(B), .pin3(C), .pin4(Kout), .pin5(1'b0), .pin6(1'b1), .pin7(_74138_1_pin7), .pin8(1'b0),
    .pin9(_74138_1_pin9), .pin10(_74138_1_pin10), .pin11(_74138_1_pin11), .pin12(_74138_1_pin12),
    .pin13(_74138_1_pin13), .pin14(_74138_1_pin14), .pin15(_74138_1_pin15), .pin16(1'b1));
  PullUp pullup_9 (.out(pullup_9_out));
  DiodeBackward diodebackward_14 (.in(F_out), .out(pullup_9_out));
  DiodeBackward diodebackward_15 (.in(F_out), .out(diodebackward_15_out));
  DiodeBackward diodebackward_16 (.in(E_out), .out(pullup_9_out));
  DiodeBackward diodebackward_17 (.in(E_out), .out(diodebackward_15_out));
  DiodeBackward diodebackward_18 (.in(D_out), .out(diodebackward_15_out));
  DiodeBackward diodebackward_19 (.in(D_out), .out(pullup_9_out));
  DiodeBackward diodebackward_20 (.in(C_out), .out(diodebackward_15_out));
  DiodeBackward diodebackward_21 (.in(C_out), .out(pullup_9_out));
  DiodeBackward diodebackward_22 (.in(B_out), .out(pullup_9_out));
  DiodeBackward diodebackward_23 (.in(A_out), .out(pullup_9_out));
  DiodeBackward diodebackward_24 (.in(_9_out), .out(pullup_9_out));
  DiodeBackward diodebackward_25 (.in(_8_out), .out(pullup_9_out));
  DiodeBackward diodebackward_26 (.in(_7_out), .out(diodebackward_15_out));
  DiodeBackward diodebackward_27 (.in(_6_out), .out(diodebackward_15_out));
  DiodeBackward diodebackward_28 (.in(_5_out), .out(diodebackward_15_out));
  DiodeBackward diodebackward_29 (.in(_4_out), .out(diodebackward_15_out));
  not not_5 (_74173_4_pin11, pullup_9_out);
  PullUp pullup_10 (.out(diodebackward_15_out));
  DiodeBackward diodebackward_30 (.in(F_out), .out(diodebackward_30_out));
  DiodeBackward diodebackward_31 (.in(E_out), .out(diodebackward_30_out));
  DiodeBackward diodebackward_32 (.in(B_out), .out(diodebackward_30_out));
  DiodeBackward diodebackward_33 (.in(A_out), .out(diodebackward_30_out));
  DiodeBackward diodebackward_34 (.in(_7_out), .out(diodebackward_30_out));
  DiodeBackward diodebackward_35 (.in(_6_out), .out(diodebackward_30_out));
  DiodeBackward diodebackward_36 (.in(_3_out), .out(diodebackward_30_out));
  DiodeBackward diodebackward_37 (.in(_2_out), .out(diodebackward_30_out));
  not not_6 (_74173_4_pin12, diodebackward_15_out);
  Monoflop monoflop_1 (.C(not_9_out), .R(1'b0), .nQ(nLATCH));  // open: Q
  PullUp pullup_11 (.out(diodebackward_30_out));
  PullUp pullup_12 (.out(pullup_12_out));
  DiodeBackward diodebackward_38 (.in(F_out), .out(pullup_12_out));
  DiodeBackward diodebackward_39 (.in(D_out), .out(pullup_12_out));
  DiodeBackward diodebackward_40 (.in(B_out), .out(pullup_12_out));
  DiodeBackward diodebackward_41 (.in(_9_out), .out(pullup_12_out));
  DiodeBackward diodebackward_42 (.in(_7_out), .out(pullup_12_out));
  DiodeBackward diodebackward_43 (.in(_5_out), .out(pullup_12_out));
  DiodeBackward diodebackward_44 (.in(_3_out), .out(pullup_12_out));
  DiodeBackward diodebackward_45 (.in(_1_out), .out(pullup_12_out));
  not not_7 (_74173_4_pin14, pullup_12_out);
  not not_8 (_74173_4_pin13, diodebackward_30_out);
  PullUp pullup_13 (.out(pullup_13_out));
  DiodeBackward diodebackward_46 (.in(F_out), .out(pullup_13_out));
  DiodeBackward diodebackward_47 (.in(E_out), .out(pullup_13_out));
  DiodeBackward diodebackward_48 (.in(D_out), .out(pullup_13_out));
  DiodeBackward diodebackward_49 (.in(C_out), .out(pullup_13_out));
  DiodeBackward diodebackward_50 (.in(B_out), .out(pullup_13_out));
  DiodeBackward diodebackward_51 (.in(A_out), .out(pullup_13_out));
  DiodeBackward diodebackward_52 (.in(_9_out), .out(pullup_13_out));
  DiodeBackward diodebackward_53 (.in(_8_out), .out(pullup_13_out));
  DiodeBackward diodebackward_54 (.in(_7_out), .out(pullup_13_out));
  DiodeBackward diodebackward_55 (.in(_6_out), .out(pullup_13_out));
  DiodeBackward diodebackward_56 (.in(_5_out), .out(pullup_13_out));
  DiodeBackward diodebackward_57 (.in(_4_out), .out(pullup_13_out));
  DiodeBackward diodebackward_58 (.in(_3_out), .out(pullup_13_out));
  DiodeBackward diodebackward_59 (.in(_2_out), .out(pullup_13_out));
  DiodeBackward diodebackward_60 (.in(_1_out), .out(pullup_13_out));
  DiodeBackward diodebackward_61 (.in(_0_out), .out(pullup_13_out));
  not not_9 (not_9_out, pullup_13_out);
  _74595 U17 (
    .pin1(A14), .pin2(A13), .pin3(A12), .pin4(A11), .pin5(A10), .pin6(A9), .pin7(A8), .pin8(1'b0),
    .pin9(U17_pin9), .pin10(nCLRPC), .pin11(GCLK), .pin12(T0), .pin13(1'b0), .pin14(PCin), .pin15(A15),
    .pin16(1'b1));
  _27C1024 U3 (
    .nCE(1'b0), .nOE(1'b0), .VPP(1'b1), .VDD(1'b1), .GND(1'b0), .I_O0(D0), .I_O1(D1), .I_O2(D2), .I_O3(D3),
    .I_O4(D4), .I_O5(D5), .I_O6(D6), .I_O7(D7), .A0(A0), .A1(A1), .A2(A2), .A3(A3), .A4(A4), .A5(A5),
    .A6(A6), .A7(A7), .A8(A8), .A9(A9), .A10(A10), .A11(A11), .A12(A12), .A13(A13), .A14(A14), .A15(A15),
    .I_O8(IR0), .I_O9(IR1), .I_O10(IR2), .I_O11(IR3), .I_O12(IR4), .I_O13(IR5), .I_O14(IR6), .I_O15(IR7),
    .VSS(1'b0));
  DiodeForward diodeforward_1 (.in(BUS15), .out(Zin));
  DiodeForward diodeforward_2 (.in(BUS14), .out(Zin));
  DiodeForward diodeforward_3 (.in(BUS13), .out(Zin));
  DiodeForward diodeforward_4 (.in(BUS12), .out(Zin));
  DiodeForward diodeforward_5 (.in(BUS11), .out(Zin));
  DiodeForward diodeforward_6 (.in(BUS10), .out(Zin));
  DiodeForward diodeforward_7 (.in(BUS9), .out(Zin));
  DiodeForward diodeforward_8 (.in(BUS8), .out(Zin));
  DiodeForward diodeforward_9 (.in(BUS7), .out(Zin));
  DiodeForward diodeforward_10 (.in(BUS6), .out(Zin));
  DiodeForward diodeforward_11 (.in(BUS5), .out(Zin));
  DiodeForward diodeforward_12 (.in(BUS4), .out(Zin));
  DiodeForward diodeforward_13 (.in(BUS3), .out(Zin));
  DiodeForward diodeforward_14 (.in(BUS2), .out(Zin));
  DiodeForward diodeforward_15 (.in(BUS1), .out(Zin));
  DiodeForward diodeforward_16 (.in(BUS0), .out(Zin));
  LED led_1 (.in(Zin));
  PullDown pulldown_1 (.out(Zin));
  _74595 U18 (
    .pin1(A6), .pin2(A5), .pin3(A4), .pin4(A3), .pin5(A2), .pin6(A1), .pin7(A0), .pin8(1'b0), .pin9(PCout),
    .pin10(nCLRPC), .pin11(GCLK), .pin12(T0), .pin13(1'b0), .pin14(U17_pin9), .pin15(A7), .pin16(1'b1));
  _74161 U20 (
    .pin1(RST), .pin2(clk), .pin3(1'b0), .pin4(1'b0), .pin5(1'b0), .pin6(1'b0), .pin7(1'b1), .pin8(1'b0),
    .pin9(1'b1), .pin10(1'b1), .pin11(U20_pin11[3]), .pin12(U20_pin11[2]), .pin13(U20_pin11[1]),
    .pin14(U20_pin11[0]), .pin15(RCO), .pin16(1'b1));
  _74138 U2 (
    .pin1(in_4), .pin2(in_5), .pin3(in_6), .pin4(1'b0), .pin5(1'b0), .pin6(1'b1), .pin7(nJMP), .pin8(1'b0),
    .pin9(ST), .pin10(SUB), .pin11(ADD), .pin12(XOR), .pin13(OR), .pin14(AND), .pin15(LOAD), .pin16(1'b1));
  PullUp pullup_14 (.out(pullup_14_out));
  DiodeBackward diodebackward_62 (.in(LOAD), .out(pullup_14_out));
  DiodeBackward diodebackward_63 (.in(LOAD), .out(diodebackward_63_out));
  DiodeBackward diodebackward_64 (.in(ADD), .out(diodebackward_63_out));
  DiodeBackward diodebackward_65 (.in(SUB), .out(diodebackward_63_out));
  DiodeBackward diodebackward_66 (.in(nJMP), .out(diodebackward_63_out));
  DiodeBackward diodebackward_67 (.in(nJMP), .out(pullup_14_out));
  Seven_Seg_Hex seven_seg_hex_5 (.d({A15, A14, A13, A12}), .dp(1'b0));
  Seven_Seg_Hex seven_seg_hex_6 (.d(U20_pin11), .dp(1'b0));
  PullUp pullup_15 (.out(diodebackward_63_out));
  DiodeBackward diodebackward_68 (.in(SUB), .out(diodebackward_68_out));
  Seven_Seg_Hex seven_seg_hex_7 (.d({A11, A10, A9, A8}), .dp(1'b0));
  LED led_2 (.in(RUN));
  PullUp pullup_16 (.out(diodebackward_68_out));
  PullUp pullup_17 (.out(pullup_17_out));
  DiodeBackward diodebackward_69 (.in(SUB), .out(pullup_17_out));
  Seven_Seg_Hex seven_seg_hex_8 (.d({A7, A6, A5, A4}), .dp(1'b0));
  _7474 U19 (
    .pin1(1'b1), .pin2(RCO), .pin3(clk), .pin4(1'b1), .pin5(RUN), .pin6(T0), .pin7(1'b0), .pin9(PC_Cin),
    .pin10(nLD), .pin11(GCLK), .pin12(PC_Carry), .pin13(1'b1), .pin14(1'b1));  // open: pin8
  PullUp pullup_18 (.out(pullup_18_out));
  DiodeBackward diodebackward_70 (.in(AND), .out(diodebackward_70_out));
  DiodeBackward diodebackward_71 (.in(OR), .out(diodebackward_70_out));
  Seven_Seg_Hex seven_seg_hex_9 (.d({A3, A2, A1, A0}), .dp(1'b0));
  PullUp pullup_19 (.out(diodebackward_70_out));
  DiodeBackward diodebackward_72 (.in(LOAD), .out(diodebackward_72_out));
  DiodeBackward diodebackward_73 (.in(OR), .out(diodebackward_72_out));
  DiodeBackward diodebackward_74 (.in(XOR), .out(diodebackward_72_out));
  DiodeBackward diodebackward_75 (.in(ADD), .out(diodebackward_72_out));
  DiodeBackward diodebackward_76 (.in(SUB), .out(diodebackward_72_out));
  DiodeBackward diodebackward_77 (.in(ST), .out(diodebackward_72_out));
  DiodeBackward diodebackward_78 (.in(nJMP), .out(diodebackward_72_out));
  PullUp pullup_20 (.out(diodebackward_72_out));
  _74540 U3_2 (
    .pin1(1'b0), .pin2(diodebackward_72_out), .pin3(diodebackward_70_out), .pin4(pullup_18_out),
    .pin5(pullup_17_out), .pin6(diodebackward_68_out), .pin7(diodebackward_63_out), .pin8(pullup_14_out),
    .pin9(Zin), .pin10(1'b0), .pin11(ZERO), .pin12(CLA), .pin13(F), .pin14(C_t), .pin15(nB), .pin16(nA),
    .pin17(I1), .pin18(I0), .pin19(1'b0), .pin20(1'b1));
  _74164 U10 (
    .pin1(1'b1), .pin2(Fout), .pin3(Ac15), .pin4(Ac14), .pin5(Ac13), .pin6(Ac12), .pin7(1'b0), .pin8(GCLK),
    .pin9(CLR), .pin10(Ac11), .pin11(Ac10), .pin12(Ac9), .pin13(Ac8), .pin14(1'b1));
  nand nand_3 (nand_3_out, clk, clk);
  xor xor_1 (xor_1_out, Ac0, nA);
  xor xor_2 (xor_2_out, nB, Bout);
  nand nand_4 (SetC_t, SETC, C_t);
  nand nand_5 (nand_5_out, C_t, C_t);
  nand nand_6 (CLR, CLA, LD);
  Seven_Seg_Hex seven_seg_hex_10 (.d({Ac15, Ac14, Ac13, Ac12}), .dp(1'b0));
  nand nand_7 (GCLK, nand_3_out, RST);
  nand nand_8 (RST, GO, nand_9_out);
  nand nand_9 (nand_9_out, RST, T0);
  Seven_Seg_Hex seven_seg_hex_11 (.d({Ac11, Ac10, Ac9, Ac8}), .dp(1'b0));
  xor xor_3 (xor_3_out, xor_1_out, xor_2_out);
  nand nand_10 (ResC, nand_5_out, LD);
  Seven_Seg_Hex seven_seg_hex_12 (.d({Ac7, Ac6, Ac5, Ac4}), .dp(1'b0));
  nand nand_11 (nand_11_out, xor_3_out, Cin);
  nand nand_12 (nand_12_out, xor_1_out, xor_2_out);
  Seven_Seg_Hex seven_seg_hex_13 (.d({Ac3, Ac2, Ac1, Ac0}), .dp(1'b0));
  _74164 U11 (
    .pin1(1'b1), .pin2(Ac8), .pin3(Ac7), .pin4(Ac6), .pin5(Ac5), .pin6(Ac4), .pin7(1'b0), .pin8(GCLK),
    .pin9(CLR), .pin10(Ac3), .pin11(Ac2), .pin12(Ac1), .pin13(Ac0), .pin14(1'b1));
  xor xor_4 (xor_4_out, xor_3_out, Cin);
  LED led_3 (.in(Cin));
  nand nand_13 (nand_13_out, nand_11_out, nand_12_out);
  _7474 U20_2 (
    .pin1(ResC), .pin2(Cout), .pin3(GCLK), .pin4(SetC_t), .pin5(Cin), .pin7(1'b0), .pin8(T0), .pin9(IX),
    .pin10(1'b1), .pin11(clk), .pin12(RCO), .pin13(1'b1), .pin14(1'b1));  // open: pin6
  xor xor_5 (PC_plus_1, PCout, PC_Cin);
  nand nand_14 (nand_14_out, PCout, PC_Cin);
  nand nand_15 (nand_15_out, xor_4_out, I0);
  nand nand_16 (nand_16_out, I1, nand_13_out);
  nand nand_17 (nand_17_out, nand_13_out, F);
  not not_10 (not_10_out, nJMP);
  not not_11 (PC_Carry, nand_14_out);
  Monoflop monoflop_2 (.C(button_1_out), .R(1'b0), .Q(LD), .nQ(nLD));
  Button button_1 (.out(button_1_out));
  Seven_Seg_Hex seven_seg_hex_14 (.d({IR7, IR6, IR5, IR4}), .dp(1'b0));
  Seven_Seg_Hex seven_seg_hex_15 (.d({BUS15, BUS14, BUS13, BUS12}), .dp(1'b0));
  nand nand_18 (nand_18_out, PC_plus_1, nJMP);
  nand nand_19 (nand_19_out, not_10_out, Fout);
  nand nand_20 (Fout, nand_15_out, nand_16_out);
  nand nand_21 (Cout, nand_17_out, nand_17_out);
  Seven_Seg_Hex seven_seg_hex_16 (.d({IR3, IR2, IR1, IR0}), .dp(1'b0));
  Seven_Seg_Hex seven_seg_hex_17 (.d({BUS11, BUS10, BUS9, BUS8}), .dp(1'b0));
  Monoflop monoflop_3 (.C(nLD), .R(1'b0), .Q(SETC), .nQ(GO));
  Seven_Seg_Hex seven_seg_hex_18 (.d({D7, D6, D5, D4}), .dp(1'b0));
  Seven_Seg_Hex seven_seg_hex_19 (.d({BUS7, BUS6, BUS5, BUS4}), .dp(1'b0));
  nand nand_22 (PCin, nand_18_out, nand_19_out);
  Monoflop monoflop_4 (.C(button_2_out), .R(1'b0), .nQ(nCLRPC));  // open: Q
  Button button_2 (.out(button_2_out));
  Seven_Seg_Hex seven_seg_hex_20 (.d({D3, D2, D1, D0}), .dp(1'b0));
  Seven_Seg_Hex seven_seg_hex_21 (.d({BUS3, BUS2, BUS1, BUS0}), .dp(1'b0));
  _74595 U19_2 (
    .pin1(MA14), .pin2(MA13), .pin3(MA12), .pin4(MA11), .pin5(MA10), .pin6(MA9), .pin7(MA8), .pin8(1'b0),
    .pin9(U19_2_pin9), .pin10(nCLRPC), .pin11(GCLK), .pin12(T0), .pin13(1'b0), .pin14(Fout), .pin15(MA15),
    .pin16(1'b1));
  _74595 U19_3 (
    .pin1(BUS14), .pin2(BUS13), .pin3(BUS12), .pin4(BUS11), .pin5(BUS10), .pin6(BUS9), .pin7(BUS8),
    .pin8(1'b0), .pin9(U19_3_pin9), .pin10(nCLRPC), .pin11(GCLK), .pin12(T0), .pin13(in_10), .pin14(MADout),
    .pin15(BUS15), .pin16(1'b1));
  DiodeForward diodeforward_17 (.in(BUS7), .out(diodeforward_17_out));
  DiodeForward diodeforward_18 (.in(BUS6), .out(diodeforward_17_out));
  DiodeForward diodeforward_19 (.in(BUS5), .out(diodeforward_17_out));
  DiodeForward diodeforward_20 (.in(BUS4), .out(diodeforward_17_out));
  DiodeForward diodeforward_21 (.in(BUS3), .out(diodeforward_17_out));
  DiodeForward diodeforward_22 (.in(BUS2), .out(diodeforward_17_out));
  DiodeForward diodeforward_23 (.in(BUS1), .out(diodeforward_17_out));
  DiodeForward diodeforward_24 (.in(BUS0), .out(diodeforward_17_out));
  PullDown pulldown_2 (.out(diodeforward_17_out));
  _74157 _74157_1 (
    .pin1(nSWITCH_RAM), .pin2(Kout), .pin3(RAMout), .pin4(Bout), .pin5(in_25), .pin6(in_26),
    .pin7(_74157_1_pin7), .pin8(1'b0), .pin9(_74157_1_pin9), .pin10(in_29), .pin11(in_30),
    .pin12(_74157_1_pin12), .pin13(in_31), .pin14(in_32), .pin15(in_28), .pin16(1'b1));
  _74139 _74139_2 (
    .pin1(in_22), .pin2(in_23), .pin3(in_24), .pin4(_74139_2_pin4), .pin5(_74139_2_pin5),
    .pin6(_74139_2_pin6), .pin7(_74139_2_pin7), .pin8(1'b0), .pin13(1'b1), .pin14(1'b1), .pin15(1'b1),
    .pin16(1'b1));  // open: pin9, pin10, pin11, pin12
  DiodeForward diodeforward_25 (.in(BUS8), .out(diodeforward_17_out));
  DiodeForward diodeforward_26 (.in(BUS9), .out(diodeforward_17_out));
  DiodeForward diodeforward_27 (.in(BUS10), .out(diodeforward_17_out));
  DiodeForward diodeforward_28 (.in(BUS11), .out(diodeforward_17_out));
  DiodeForward diodeforward_29 (.in(BUS12), .out(diodeforward_17_out));
  DiodeForward diodeforward_30 (.in(BUS13), .out(diodeforward_17_out));
  DiodeForward diodeforward_31 (.in(BUS14), .out(diodeforward_17_out));
  DiodeForward diodeforward_32 (.in(BUS15), .out(diodeforward_17_out));
  _74595 U20_3 (
    .pin1(MA6), .pin2(MA5), .pin3(MA4), .pin4(MA3), .pin5(MA2), .pin6(MA1), .pin7(MA0), .pin8(1'b0),
    .pin9(MADout), .pin10(nCLRPC), .pin11(GCLK), .pin12(T0), .pin13(1'b0), .pin14(U19_2_pin9), .pin15(MA7),
    .pin16(1'b1));
  _74595 U20_4 (
    .pin1(BUS6), .pin2(BUS5), .pin3(BUS4), .pin4(BUS3), .pin5(BUS2), .pin6(BUS1), .pin7(BUS0), .pin8(1'b0),
    .pin9(U20_4_pin9), .pin10(nCLRPC), .pin11(GCLK), .pin12(T0), .pin13(in_10), .pin14(U19_3_pin9),
    .pin15(BUS7), .pin16(1'b1));
  _74165 U8 (
    .pin1(in_11), .pin2(GCLK), .pin3(BUS11), .pin4(BUS10), .pin5(BUS9), .pin6(BUS8), .pin8(1'b0),
    .pin9(U8_pin9), .pin10(1'b0), .pin11(BUS15), .pin12(BUS14), .pin13(BUS13), .pin14(BUS12), .pin15(1'b0),
    .pin16(1'b1));  // open: pin7
  _74165 U9 (
    .pin1(in_11), .pin2(GCLK), .pin3(BUS3), .pin4(BUS2), .pin5(BUS1), .pin6(BUS0), .pin8(1'b0),
    .pin9(RAMout), .pin10(U8_pin9), .pin11(BUS7), .pin12(BUS6), .pin13(BUS5), .pin14(BUS4), .pin15(1'b0),
    .pin16(1'b1));  // open: pin7
  Seven_Seg_Hex seven_seg_hex_22 (.d({MA15, MA14, MA13, MA12}), .dp(1'b0));
  Seven_Seg_Hex seven_seg_hex_23 (.d({BUS15, BUS14, BUS13, BUS12}), .dp(1'b0));
  Seven_Seg_Hex seven_seg_hex_24 (.d({MA11, MA10, MA9, MA8}), .dp(1'b0));
  Seven_Seg_Hex seven_seg_hex_25 (.d({BUS11, BUS10, BUS9, BUS8}), .dp(1'b0));
  _62256 U10_2 (
    .A0(MA0), .A1(MA1), .A2(MA2), .A3(MA3), .A4(MA4), .A5(MA5), .A6(MA6), .A7(MA7), .A8(MA8), .A9(MA9),
    .A10(MA10), .A11(MA11), .A12(MA12), .nCE(1'b0), .nOE(in_11), .nWE(in_10), .D0(BUS8), .D1(BUS9),
    .D2(BUS10), .D3(BUS11), .D4(BUS12), .D5(BUS13), .D6(BUS14), .D7(BUS15), .VCC(1'b1), .GND(1'b0),
    .A13(MA13), .A14(MA14));
  _62256 U11_2 (
    .A0(MA0), .A1(MA1), .A2(MA2), .A3(MA3), .A4(MA4), .A5(MA5), .A6(MA6), .A7(MA7), .A8(MA8), .A9(MA9),
    .A10(MA10), .A11(MA11), .A12(MA12), .nCE(1'b0), .nOE(in_11), .nWE(in_10), .D0(BUS0), .D1(BUS1),
    .D2(BUS2), .D3(BUS3), .D4(BUS4), .D5(BUS5), .D6(BUS6), .D7(BUS7), .VCC(1'b1), .GND(1'b0), .A13(MA13),
    .A14(MA14));
  Seven_Seg_Hex seven_seg_hex_26 (.d({MA7, MA6, MA5, MA4}), .dp(1'b0));
  Seven_Seg_Hex seven_seg_hex_27 (.d({BUS7, BUS6, BUS5, BUS4}), .dp(1'b0));
  Seven_Seg_Hex seven_seg_hex_28 (.d({MA3, MA2, MA1, MA0}), .dp(1'b0));
  Seven_Seg_Hex seven_seg_hex_29 (.d({BUS3, BUS2, BUS1, BUS0}), .dp(1'b0));

  assign nCE = in_12;
  assign nRD = in_11;
  assign nWR = in_10;

  // Other names for the same wires on the sheet: Aout = Ac0; nLD_INC = nJMP; nload_t = in_11; nOE = in_11;
  //   nRRES = nCLRPC; nstore = in_10; nWE = in_10; R0 = D0; R1 = D1; R2 = D2; R3 = D3; R4 = D4; R5 = D5; R6 = D6;
  //   R7 = D7; R8 = IR0; R9 = IR1; R10 = IR2; R11 = IR3; R12 = IR4; R13 = IR5; R14 = IR6; R15 = IR7; Rout = in_18

  // Notes on the sheet:
  //   clk: Hz: 20
  //   in_10: default 1
  //   in_11: default 1
  //   in_12: default 1
  //   nCE: default 1
  //   nRD: default 1
  //   nWR: default 1
  //   Front Panel
  //   LOAD
  //   UP
  //   DOWN
  //   ~DE
  //   COUNT
  //   WRITE
  //   READ
  //   RESET
  //   Hex Keypad
  //   Keypad read register K
  //   Data Input
  //   KEY DATA
  //   KEYSWITCH REGISTER
  //   MEMORY  ADDRESS REGISTER
  //   Instruction Input
  //   Instruction ROM
  //   ZERO
  //   Clock Sequencer 3 packages
  //   Clock #
  //   CLA
  //   Instruction Decode
  //   PROGRAM COUNTER
  //   F
  //   ~B
  //   C
  //   Carry FF
  //   ~A
  //   I1
  //   I0
  //   AND
  //   OR
  //   XOR
  //   ADD
  //   SUB
  //   STORE
  //   JMP
  //   U21A
  //   ALU
  //   16 bit Shift Register A
  //   CLR ACC
  //   U21B
  //   U21C
  //   U21D
  //   ACCUMULATOR
  //   CARRY
  //   Spider 16-bit Serial CPU
  //   Program Counter (Incrementer)  3.5 packages
  //   U26A
  //   U22A
  //   Any residual carry is cleared before an operation
  //   Carry is only set before Bit 0 of an operation
  //   Suppress Carry
  //   INSTRUCTION
  //   DATA BUS
  //   U22C
  //   U22B
  //   CLR PC
  //   U22D
  //   DATA
  //   Memory Sub Module 32K x 16-bit SRAM
  //   SOURCE SELECT
  //   MEMORY  WRITE REGISTER
  //   MEMORY READ RGISTER
  //   RAM ADDRESS
  //   RAM DATA
  //   RAM HI
  //   RAM LO
endmodule
