// Digital circuit spider007.dig as structural Verilog
module spider007 (
  input  clk,
  input  in_2,
  input  in_3,
  input  in_4,
  input  in_5,
  input  in_6,
  input  in_7
);

  wire AC0, AC1, AC2, AC3, AC4, AC5, AC6, AC7, AC8, AC9, AC10, AC11, AC12, AC13, AC14, AC15, ADD, AND,
       and_2_out, Aout, Bout, BUS0, BUS1, BUS2, BUS3, BUS4, BUS5, BUS6, BUS7, BUS8, BUS9, BUS10, BUS11,
       BUS12, BUS13, BUS14, BUS15, button_1_out, button_2_out, button_3_out, button_4_out, button_5_out,
       button_6_out, button_7_out, button_8_out, button_9_out, button_10_out, button_11_out, button_12_out,
       button_13_out, button_14_out, button_15_out, button_16_out, C, Cin, CLA, CLR, Cout, d_ff_1_nq,
       d_ff_2_nq, d_ff_3_nq, d_ff_4_nq, d_ff_5_nq, d_ff_6_nq, d_ff_7_nq, d_ff_8_nq, d_ff_9_nq, d_ff_10_nq,
       d_ff_11_nq, d_ff_12_nq, diodebackward_1_out, diodebackward_5_out, diodeforward_1_out, F, Fout, GCLK,
       I0, I1, I4, I5, I6, I7, IC18_2_nq, IC18_nq, IC19_2_nq, IC19_nq, INCPC, LDA, LOAD, MAR0, MAR1, MAR2,
       MAR3, MAR4, MAR5, MAR6, MAR7, MAR8, MAR9, MAR10, MAR11, nA, nand_1_out, nand_2_out, nand_4_out,
       nand_5_out, nand_7_out, nand_9_out, nand_10_out, nand_11_out, nand_12_out, nand_13_out, nand_14_out,
       nand_17_out, nand_19_out, nB, nCLRPC, nJMP, nLDB, nOE, not_1_out, nQ3, nQ4, nRST, nTP0, nTP1, nTP3,
       nTP4, nTP5, nTP7, nWE, nZERO, OR, PC0, PC1, PC2, PC3, PC4, PC5, PC6, PC7, PC8, PC9, PC10, PC11, PC12,
       PC13, PC14, PC15, pullup_1_out, pullup_3_out, pullup_5_out, pullup_6_out, pullup_7_out, Q3, Q4, RCO,
       SETC, ST, SUB, T0, U3_pin11, U3_pin12, U3_pin13, U3_pin14, U3_pin15, U4_pin11, U4_pin12, U4_pin13,
       U4_pin14, U4_pin15, U5_pin11, U5_pin12, U5_pin13, U5_pin14, U5_pin15, U6_pin11, U6_pin12, U6_pin13,
       U6_pin14, U8_2_pin9, U15_pin9, U16_pin9, U31_pin15, XOR, xor_1_out, xor_2_out, xor_3_out, xor_4_out,
       Y12, Y13, Y14, Y15;
  wire [2:0] U19_pin14;
  wire [3:0] IC18_q, IC19_q, U13_pin3, U13_pin13, U14_pin4, U17_pin6, U18_pin6;
  wire [3:1] U14_pin10;

  not not_1 (not_1_out, in_7);
  _74161 U3 (
    .pin1(nCLRPC), .pin2(INCPC), .pin3(BUS0), .pin4(BUS1), .pin5(BUS2), .pin6(BUS3), .pin7(1'b1),
    .pin8(1'b0), .pin9(nJMP), .pin10(1'b1), .pin11(U3_pin11), .pin12(U3_pin12), .pin13(U3_pin13),
    .pin14(U3_pin14), .pin15(U3_pin15), .pin16(1'b1));
  _74161 U4 (
    .pin1(nCLRPC), .pin2(INCPC), .pin3(BUS4), .pin4(BUS5), .pin5(BUS6), .pin6(BUS7), .pin7(1'b1),
    .pin8(1'b0), .pin9(nJMP), .pin10(U3_pin15), .pin11(U4_pin11), .pin12(U4_pin12), .pin13(U4_pin13),
    .pin14(U4_pin14), .pin15(U4_pin15), .pin16(1'b1));
  _74161 U5 (
    .pin1(nCLRPC), .pin2(INCPC), .pin3(BUS8), .pin4(BUS9), .pin5(BUS10), .pin6(BUS11), .pin7(1'b1),
    .pin8(1'b0), .pin9(in_2), .pin10(U4_pin15), .pin11(U5_pin11), .pin12(U5_pin12), .pin13(U5_pin13),
    .pin14(U5_pin14), .pin15(U5_pin15), .pin16(1'b1));
  _74161 U6 (
    .pin1(nCLRPC), .pin2(INCPC), .pin3(in_3), .pin4(in_4), .pin5(in_5), .pin6(in_6), .pin7(1'b1),
    .pin8(1'b0), .pin9(in_2), .pin10(U5_pin15), .pin11(U6_pin11), .pin12(U6_pin12), .pin13(U6_pin13),
    .pin14(U6_pin14), .pin16(1'b1));  // open: pin15
  _74173 U7 (
    .pin1(not_1_out), .pin2(not_1_out), .pin3(MAR0), .pin4(MAR1), .pin5(MAR2), .pin6(MAR3), .pin7(nTP4),
    .pin8(1'b0), .pin9(1'b0), .pin10(1'b0), .pin11(BUS3), .pin12(BUS2), .pin13(BUS1), .pin14(BUS0),
    .pin15(1'b0), .pin16(1'b1));
  _74173 U8 (
    .pin1(not_1_out), .pin2(not_1_out), .pin3(MAR4), .pin4(MAR5), .pin5(MAR6), .pin6(MAR7), .pin7(nTP4),
    .pin8(1'b0), .pin9(1'b0), .pin10(1'b0), .pin11(BUS7), .pin12(BUS6), .pin13(BUS5), .pin14(BUS4),
    .pin15(1'b0), .pin16(1'b1));
  _74173 U9 (
    .pin1(not_1_out), .pin2(not_1_out), .pin3(MAR8), .pin4(MAR9), .pin5(MAR10), .pin6(MAR11), .pin7(nTP4),
    .pin8(1'b0), .pin9(1'b0), .pin10(1'b0), .pin11(BUS11), .pin12(BUS10), .pin13(BUS9), .pin14(BUS8),
    .pin15(1'b0), .pin16(1'b1));
  _74541 U1 (
    .pin1(in_7), .pin2(U3_pin14), .pin3(U3_pin13), .pin4(U3_pin12), .pin5(U3_pin11), .pin6(U4_pin14),
    .pin7(U4_pin13), .pin8(U4_pin12), .pin9(U4_pin11), .pin10(1'b0), .pin11(PC7), .pin12(PC6), .pin13(PC5),
    .pin14(PC4), .pin15(PC3), .pin16(PC2), .pin17(PC1), .pin18(PC0), .pin19(1'b0), .pin20(1'b1));
  _74541 U2 (
    .pin1(in_7), .pin2(U5_pin14), .pin3(U5_pin13), .pin4(U5_pin12), .pin5(U5_pin11), .pin6(U6_pin14),
    .pin7(U6_pin13), .pin8(U6_pin12), .pin9(U6_pin11), .pin10(1'b0), .pin11(PC15), .pin12(PC14),
    .pin13(PC13), .pin14(PC12), .pin15(PC11), .pin16(PC10), .pin17(PC9), .pin18(PC8), .pin19(1'b0),
    .pin20(1'b1));
  _62256 U11 (
    .A0(PC0), .A1(PC1), .A2(PC2), .A3(PC3), .A4(PC4), .A5(PC5), .A6(PC6), .A7(PC7), .A8(PC8), .A9(PC9),
    .A10(PC10), .A11(PC11), .A12(PC12), .nCE(1'b1), .nOE(nOE), .nWE(nWE), .D0(BUS8), .D1(BUS9), .D2(BUS10),
    .D3(BUS11), .D4(BUS12), .D5(BUS13), .D6(BUS14), .D7(BUS15), .VCC(1'b1), .GND(1'b0), .A13(PC13), .A14(PC14));
  _62256 U12 (
    .A0(PC0), .A1(PC1), .A2(PC2), .A3(PC3), .A4(PC4), .A5(PC5), .A6(PC6), .A7(PC7), .A8(PC8), .A9(PC9),
    .A10(PC10), .A11(PC11), .A12(PC12), .nCE(1'b1), .nOE(nOE), .nWE(nWE), .D0(BUS0), .D1(BUS1), .D2(BUS2),
    .D3(BUS3), .D4(BUS4), .D5(BUS5), .D6(BUS6), .D7(BUS7), .VCC(1'b1), .GND(1'b0), .A13(PC13), .A14(PC14));
  Seven_Seg_Hex seven_seg_hex_1 (.d(4'b0000), .dp(1'b0));
  Seven_Seg_Hex seven_seg_hex_2 (.d({MAR11, MAR10, MAR9, MAR8}), .dp(1'b0));
  Seven_Seg_Hex seven_seg_hex_3 (.d({MAR7, MAR6, MAR5, MAR4}), .dp(1'b0));
  Seven_Seg_Hex seven_seg_hex_4 (.d({MAR3, MAR2, MAR1, MAR0}), .dp(1'b0));
  _74173 U10 (
    .pin1(1'b0), .pin2(1'b0), .pin3(I4), .pin4(I5), .pin5(I6), .pin6(I7), .pin7(nTP4), .pin8(1'b0),
    .pin9(1'b0), .pin10(1'b0), .pin11(BUS15), .pin12(BUS14), .pin13(BUS13), .pin14(BUS12), .pin15(1'b0),
    .pin16(1'b1));
  and and_1 (LOAD, I7, U31_pin15);
  _74138 U31 (
    .pin1(I4), .pin2(I5), .pin3(I6), .pin4(1'b0), .pin5(1'b0), .pin6(I7), .pin7(nJMP), .pin8(1'b0),
    .pin9(ST), .pin10(SUB), .pin11(ADD), .pin12(XOR), .pin13(OR), .pin14(AND), .pin15(U31_pin15), .pin16(1'b1));
  Seven_Seg_Hex seven_seg_hex_5 (.d({PC15, PC14, PC13, PC12}), .dp(1'b0));
  Seven_Seg_Hex seven_seg_hex_6 (.d({PC11, PC10, PC9, PC8}), .dp(1'b0));
  DiodeBackward diodebackward_1 (.in(LOAD), .out(diodebackward_1_out));
  Seven_Seg_Hex seven_seg_hex_7 (.d({PC7, PC6, PC5, PC4}), .dp(1'b0));
  PullUp pullup_1 (.out(pullup_1_out));
  PullUp pullup_2 (.out(diodebackward_1_out));
  DiodeBackward diodebackward_2 (.in(LOAD), .out(pullup_1_out));
  DiodeBackward diodebackward_3 (.in(ADD), .out(pullup_1_out));
  DiodeBackward diodebackward_4 (.in(SUB), .out(pullup_1_out));
  Seven_Seg_Hex seven_seg_hex_8 (.d({PC3, PC2, PC1, PC0}), .dp(1'b0));
  PullUp pullup_3 (.out(pullup_3_out));
  DiodeBackward diodebackward_5 (.in(SUB), .out(diodebackward_5_out));
  DiodeBackward diodebackward_6 (.in(SUB), .out(pullup_3_out));
  PullUp pullup_4 (.out(diodebackward_5_out));
  Seven_Seg_Hex seven_seg_hex_9 (.d({BUS15, BUS14, BUS13, BUS12}), .dp(1'b0));
  _27C1024 U33 (
    .nCE(1'b0), .nOE(1'b0), .VPP(1'b1), .VDD(1'b1), .GND(1'b0), .I_O0(BUS0), .I_O1(BUS1), .I_O2(BUS2),
    .I_O3(BUS3), .I_O4(BUS4), .I_O5(BUS5), .I_O6(BUS6), .I_O7(BUS7), .A0(PC0), .A1(PC1), .A2(PC2), .A3(PC3),
    .A4(PC4), .A5(PC5), .A6(PC6), .A7(PC7), .A8(PC8), .A9(PC9), .A10(PC10), .A11(PC11), .A12(PC12),
    .A13(PC13), .A14(PC14), .A15(PC15), .I_O8(BUS8), .I_O9(BUS9), .I_O10(BUS10), .I_O11(BUS11),
    .I_O12(BUS12), .I_O13(BUS13), .I_O14(BUS14), .I_O15(BUS15), .VSS(1'b0));
  PullUp pullup_5 (.out(pullup_5_out));
  PullUp pullup_6 (.out(pullup_6_out));
  DiodeBackward diodebackward_7 (.in(AND), .out(pullup_6_out));
  DiodeBackward diodebackward_8 (.in(OR), .out(pullup_6_out));
  DiodeBackward diodebackward_9 (.in(nJMP), .out(pullup_6_out));
  Seven_Seg_Hex seven_seg_hex_10 (.d({BUS11, BUS10, BUS9, BUS8}), .dp(1'b0));
  PullUp pullup_7 (.out(pullup_7_out));
  DiodeBackward diodebackward_10 (.in(LOAD), .out(pullup_7_out));
  DiodeBackward diodebackward_11 (.in(OR), .out(pullup_7_out));
  DiodeBackward diodebackward_12 (.in(XOR), .out(pullup_7_out));
  DiodeBackward diodebackward_13 (.in(ADD), .out(pullup_7_out));
  DiodeBackward diodebackward_14 (.in(SUB), .out(pullup_7_out));
  DiodeBackward diodebackward_15 (.in(ST), .out(pullup_7_out));
  DiodeBackward diodebackward_16 (.in(nJMP), .out(pullup_7_out));
  Seven_Seg_Hex seven_seg_hex_11 (.d({BUS7, BUS6, BUS5, BUS4}), .dp(1'b0));
  _74540 U32 (
    .pin1(1'b0), .pin2(pullup_7_out), .pin3(pullup_6_out), .pin4(pullup_5_out), .pin5(diodebackward_5_out),
    .pin6(pullup_3_out), .pin7(pullup_1_out), .pin8(diodebackward_1_out), .pin9(1'b0), .pin10(1'b0),
    .pin12(CLA), .pin13(F), .pin14(C), .pin15(nB), .pin16(nA), .pin17(I1), .pin18(I0), .pin19(1'b0),
    .pin20(1'b1));  // open: pin11
  Seven_Seg_Hex seven_seg_hex_12 (.d({BUS3, BUS2, BUS1, BUS0}), .dp(1'b0));
  and and_2 (and_2_out, CLR, nCLRPC);
  _74595 U8_2 (
    .pin1(AC14), .pin2(AC13), .pin3(AC12), .pin4(AC11), .pin5(AC10), .pin6(AC9), .pin7(AC8), .pin8(1'b0),
    .pin9(U8_2_pin9), .pin10(nTP7), .pin11(GCLK), .pin12(T0), .pin13(1'b0), .pin14(Fout), .pin15(AC15),
    .pin16(1'b1));
  // Not not_2 has open pins: in=nOE, out=open
  LED led_1 (.in(IC19_q[3]));
  D_FF IC19 (.D(IC19_nq), .C(button_1_out), .Q(IC19_q[3]), .nQ(IC19_nq));
  Button button_1 (.out(button_1_out));
  _74164 U13 (
    .pin1(1'b1), .pin2(Fout), .pin3(U13_pin3[3]), .pin4(U13_pin3[2]), .pin5(U13_pin3[1]), .pin6(U13_pin3[0]),
    .pin7(1'b0), .pin8(GCLK), .pin9(and_2_out), .pin10(U13_pin13[3]), .pin11(U13_pin13[2]),
    .pin12(U13_pin13[1]), .pin13(U13_pin13[0]), .pin14(1'b1));
  LED led_2 (.in(IC19_q[2]));
  D_FF d_ff_1 (.D(d_ff_1_nq), .C(button_2_out), .Q(IC19_q[2]), .nQ(d_ff_1_nq));
  Button button_2 (.out(button_2_out));
  _74541 U17 (
    .pin1(1'b0), .pin2(IC19_q[3]), .pin3(IC19_q[2]), .pin4(IC19_q[1]), .pin5(IC19_q[0]), .pin6(U17_pin6[3]),
    .pin7(U17_pin6[2]), .pin8(U17_pin6[1]), .pin9(U17_pin6[0]), .pin10(1'b0), .pin11(BUS8), .pin12(BUS9),
    .pin13(BUS10), .pin14(BUS11), .pin15(BUS12), .pin16(BUS13), .pin17(BUS14), .pin18(BUS15), .pin19(1'b1),
    .pin20(1'b1));
  LED led_3 (.in(IC19_q[1]));
  D_FF d_ff_2 (.D(d_ff_2_nq), .C(button_3_out), .Q(IC19_q[1]), .nQ(d_ff_2_nq));
  Button button_3 (.out(button_3_out));
  Seven_Seg_Hex seven_seg_hex_13 (.d(U13_pin3), .dp(1'b0));
  LED led_4 (.in(IC19_q[0]));
  D_FF d_ff_3 (.D(d_ff_3_nq), .C(button_4_out), .Q(IC19_q[0]), .nQ(d_ff_3_nq));
  Button button_4 (.out(button_4_out));
  Seven_Seg_Hex seven_seg_hex_14 (.d(U13_pin13), .dp(1'b0));
  LED led_5 (.in(U17_pin6[3]));
  D_FF d_ff_4 (.D(d_ff_4_nq), .C(button_5_out), .Q(U17_pin6[3]), .nQ(d_ff_4_nq));
  Button button_5 (.out(button_5_out));
  _74595 U9_2 (
    .pin1(AC6), .pin2(AC5), .pin3(AC4), .pin4(AC3), .pin5(AC2), .pin6(AC1), .pin7(AC0), .pin8(1'b0),
    .pin10(nTP7), .pin11(GCLK), .pin12(T0), .pin13(1'b0), .pin14(U8_2_pin9), .pin15(AC7), .pin16(1'b1));  // open: pin9
  Seven_Seg_Hex seven_seg_hex_15 (.d(U14_pin4), .dp(1'b0));
  LED led_6 (.in(U17_pin6[2]));
  D_FF d_ff_5 (.D(d_ff_5_nq), .C(button_6_out), .Q(U17_pin6[2]), .nQ(d_ff_5_nq));
  Button button_6 (.out(button_6_out));
  Seven_Seg_Hex seven_seg_hex_16 (.d({U14_pin10, Aout}), .dp(1'b0));
  LED led_7 (.in(U17_pin6[1]));
  D_FF d_ff_6 (.D(d_ff_6_nq), .C(button_7_out), .Q(U17_pin6[1]), .nQ(d_ff_6_nq));
  Button button_7 (.out(button_7_out));
  _74164 U14 (
    .pin1(1'b1), .pin2(U13_pin13[0]), .pin3(U14_pin4[3]), .pin4(U14_pin4[2]), .pin5(U14_pin4[1]),
    .pin6(U14_pin4[0]), .pin7(1'b0), .pin8(GCLK), .pin9(and_2_out), .pin10(U14_pin10[3]),
    .pin11(U14_pin10[2]), .pin12(U14_pin10[1]), .pin13(Aout), .pin14(1'b1));
  LED led_8 (.in(U17_pin6[0]));
  D_FF IC19_2 (.D(IC19_2_nq), .C(button_8_out), .Q(U17_pin6[0]), .nQ(IC19_2_nq));
  Button button_8 (.out(button_8_out));
  Seven_Seg_Hex seven_seg_hex_17 (.d(IC19_q), .dp(1'b0));
  DiodeForward diodeforward_1 (.in(AC15), .out(diodeforward_1_out));
  DiodeForward diodeforward_2 (.in(AC14), .out(diodeforward_1_out));
  DiodeForward diodeforward_3 (.in(AC13), .out(diodeforward_1_out));
  DiodeForward diodeforward_4 (.in(AC12), .out(diodeforward_1_out));
  DiodeForward diodeforward_5 (.in(AC11), .out(diodeforward_1_out));
  DiodeForward diodeforward_6 (.in(AC10), .out(diodeforward_1_out));
  DiodeForward diodeforward_7 (.in(AC9), .out(diodeforward_1_out));
  DiodeForward diodeforward_8 (.in(AC8), .out(diodeforward_1_out));
  DiodeForward diodeforward_9 (.in(AC7), .out(diodeforward_1_out));
  DiodeForward diodeforward_10 (.in(AC6), .out(diodeforward_1_out));
  DiodeForward diodeforward_11 (.in(AC5), .out(diodeforward_1_out));
  DiodeForward diodeforward_12 (.in(AC4), .out(diodeforward_1_out));
  DiodeForward diodeforward_13 (.in(AC3), .out(diodeforward_1_out));
  DiodeForward diodeforward_14 (.in(AC2), .out(diodeforward_1_out));
  DiodeForward diodeforward_15 (.in(AC1), .out(diodeforward_1_out));
  DiodeForward diodeforward_16 (.in(AC0), .out(diodeforward_1_out));
  Seven_Seg_Hex seven_seg_hex_18 (.d(U17_pin6), .dp(1'b0));
  Seven_Seg_Hex seven_seg_hex_19 (.d({AC15, AC14, AC13, AC12}), .dp(1'b0));
  LED led_9 (.in(diodeforward_1_out));
  PullDown pulldown_1 (.out(diodeforward_1_out));
  LED led_10 (.in(IC18_q[3]));
  D_FF IC18 (.D(IC18_nq), .C(button_9_out), .Q(IC18_q[3]), .nQ(IC18_nq));
  Seven_Seg_Hex seven_seg_hex_20 (.d({AC11, AC10, AC9, AC8}), .dp(1'b0));
  not not_3 (nZERO, diodeforward_1_out);
  LED led_11 (.in(IC18_q[2]));
  D_FF d_ff_7 (.D(d_ff_7_nq), .C(button_10_out), .Q(IC18_q[2]), .nQ(d_ff_7_nq));
  Button button_9 (.out(button_9_out));
  Seven_Seg_Hex seven_seg_hex_21 (.d({AC7, AC6, AC5, AC4}), .dp(1'b0));
  _74541 U18 (
    .pin1(1'b0), .pin2(IC18_q[3]), .pin3(IC18_q[2]), .pin4(IC18_q[1]), .pin5(IC18_q[0]), .pin6(U18_pin6[3]),
    .pin7(U18_pin6[2]), .pin8(U18_pin6[1]), .pin9(U18_pin6[0]), .pin10(1'b0), .pin11(BUS0), .pin12(BUS1),
    .pin13(BUS2), .pin14(BUS3), .pin15(BUS4), .pin16(BUS5), .pin17(BUS6), .pin18(BUS7), .pin19(1'b1),
    .pin20(1'b1));
  LED led_12 (.in(IC18_q[1]));
  D_FF d_ff_8 (.D(d_ff_8_nq), .C(button_11_out), .Q(IC18_q[1]), .nQ(d_ff_8_nq));
  Button button_10 (.out(button_10_out));
  Seven_Seg_Hex seven_seg_hex_22 (.d({AC3, AC2, AC1, AC0}), .dp(1'b0));
  LED led_13 (.in(IC18_q[0]));
  D_FF d_ff_9 (.D(d_ff_9_nq), .C(button_12_out), .Q(IC18_q[0]), .nQ(d_ff_9_nq));
  Button button_11 (.out(button_11_out));
  LED led_14 (.in(U18_pin6[3]));
  D_FF d_ff_10 (.D(d_ff_10_nq), .C(button_13_out), .Q(U18_pin6[3]), .nQ(d_ff_10_nq));
  Button button_12 (.out(button_12_out));
  LED led_15 (.in(U18_pin6[2]));
  D_FF d_ff_11 (.D(d_ff_11_nq), .C(button_14_out), .Q(U18_pin6[2]), .nQ(d_ff_11_nq));
  Button button_13 (.out(button_13_out));
  Reset reset_1 (.out(nCLRPC));
  LED led_16 (.in(U18_pin6[1]));
  D_FF d_ff_12 (.D(d_ff_12_nq), .C(button_15_out), .Q(U18_pin6[1]), .nQ(d_ff_12_nq));
  Button button_14 (.out(button_14_out));
  LED led_17 (.in(U18_pin6[0]));
  D_FF IC18_2 (.D(IC18_2_nq), .C(button_16_out), .Q(U18_pin6[0]), .nQ(IC18_2_nq));
  Button button_15 (.out(button_15_out));
  _74161 U19 (
    .pin1(nRST), .pin2(clk), .pin3(1'b0), .pin4(1'b0), .pin5(1'b0), .pin6(1'b0), .pin7(1'b1), .pin8(1'b0),
    .pin9(1'b1), .pin10(1'b1), .pin11(Q3), .pin12(U19_pin14[2]), .pin13(U19_pin14[1]), .pin14(U19_pin14[0]),
    .pin15(RCO), .pin16(1'b1));
  _74161 U20 (
    .pin1(nRST), .pin2(clk), .pin3(1'b0), .pin4(1'b0), .pin5(1'b0), .pin6(1'b0), .pin7(1'b1), .pin8(1'b0),
    .pin9(1'b1), .pin10(RCO), .pin14(Q4), .pin16(1'b1));  // open: pin11, pin12, pin13, pin15
  _74157 U34 (
    .pin1(I7), .pin2(BUS12), .pin3(1'b0), .pin4(Y12), .pin5(BUS13), .pin6(1'b0), .pin7(Y13), .pin8(1'b0),
    .pin9(Y14), .pin10(1'b0), .pin11(BUS14), .pin12(Y15), .pin13(1'b0), .pin14(BUS15), .pin15(1'b0),
    .pin16(1'b1));
  Seven_Seg_Hex seven_seg_hex_23 (.d(IC18_q), .dp(1'b0));
  Button button_16 (.out(button_16_out));
  Seven_Seg_Hex seven_seg_hex_24 (.d(U18_pin6), .dp(1'b0));
  Seven_Seg_Hex seven_seg_hex_25 (.d({3'b000, Q4}), .dp(1'b0));
  _74165 U15 (
    .pin1(nLDB), .pin2(GCLK), .pin3(BUS11), .pin4(BUS10), .pin5(BUS9), .pin6(BUS8), .pin8(1'b0),
    .pin9(U15_pin9), .pin10(1'b0), .pin11(Y15), .pin12(Y14), .pin13(Y13), .pin14(Y12), .pin15(1'b0),
    .pin16(1'b1));  // open: pin7
  xor xor_1 (xor_1_out, Aout, nA);
  xor xor_2 (xor_2_out, nB, Bout);
  nand nand_1 (nand_1_out, SETC, C);
  nand nand_2 (nand_2_out, C, C);
  nand nand_3 (CLR, CLA, LDA);
  Seven_Seg_Hex seven_seg_hex_26 (.d({Q3, U19_pin14}), .dp(1'b0));
  _74138 U21 (
    .pin1(U19_pin14[0]), .pin2(U19_pin14[1]), .pin3(U19_pin14[2]), .pin4(Q3), .pin5(Q4), .pin6(1'b1),
    .pin7(nTP7), .pin8(1'b0), .pin9(nLDB), .pin10(nTP5), .pin11(nTP4), .pin12(nTP3), .pin13(INCPC),
    .pin14(nTP1), .pin15(nTP0), .pin16(1'b1));
  nand nand_4 (nand_4_out, clk, clk);
  nand nand_5 (nand_5_out, nQ3, nQ4);
  nand nand_6 (nRST, Q3, Q4);
  nand nand_7 (nand_7_out, nand_2_out, LDA);
  xor xor_3 (xor_3_out, xor_1_out, xor_2_out);
  nand nand_8 (GCLK, nand_4_out, nand_5_out);
  _74165 U16 (
    .pin1(nLDB), .pin2(GCLK), .pin3(BUS3), .pin4(BUS2), .pin5(BUS1), .pin6(BUS0), .pin8(1'b0),
    .pin9(U16_pin9), .pin10(U15_pin9), .pin11(BUS7), .pin12(BUS6), .pin13(BUS5), .pin14(BUS4), .pin15(1'b0),
    .pin16(1'b1));  // open: pin7
  xor xor_4 (xor_4_out, xor_3_out, Cin);
  nand nand_9 (nand_9_out, xor_3_out, Cin);
  nand nand_10 (nand_10_out, xor_1_out, xor_2_out);
  nand nand_11 (nand_11_out, nand_9_out, nand_10_out);
  LED TP0 (.in(nTP0));
  LED TP1 (.in(nTP1));
  LED TP2 (.in(INCPC));
  LED TP3 (.in(nTP3));
  LED TP4 (.in(nTP4));
  LED TP5 (.in(nTP5));
  LED TP6 (.in(nLDB));
  LED TP7 (.in(nTP7));
  and and_3 (Bout, nJMP, U16_pin9);
  nand nand_12 (nand_12_out, xor_4_out, I0);
  nand nand_13 (nand_13_out, I1, nand_11_out);
  nand nand_14 (nand_14_out, nand_11_out, F);
  nand nand_15 (Fout, nand_12_out, nand_13_out);
  nand nand_16 (Cout, nand_14_out, nand_14_out);
  nand nand_17 (nand_17_out, nTP0, nWE);
  nand nand_18 (nWE, nand_17_out, INCPC);
  nand nand_19 (nand_19_out, nTP3, nOE);
  nand nand_20 (nOE, nand_19_out, nTP5);
  not not_4 (LDA, nLDB);
  not not_5 (SETC, nTP7);
  not not_6 (nQ3, Q3);
  not not_7 (nQ4, Q4);
  not not_8 (T0, nRST);
  _7474 U23 (
    .pin1(nand_7_out), .pin2(Cout), .pin3(GCLK), .pin4(nand_1_out), .pin5(Cin), .pin7(1'b0), .pin10(1'b1),
    .pin11(1'b1), .pin12(1'b1), .pin13(1'b1), .pin14(1'b1));  // open: pin6, pin8, pin9

  // Other names for the same wires on the sheet: nPCEN = in_7; nPH = in_2; nPL = nJMP; nTP2 = INCPC; nTP6 = nLDB;
  //   RES = nTP7

  // Notes on the sheet:
  //   clk: Hz: 4
  //   in_2: default 1
  //   SPIder 007 16-bit serial CPU Testbed
  //   RAM HI
  //   RAM LO
  //   MEM ADDRESS REG
  //   Instruction Input
  //   RAM ADDRESS
  //   U35A
  //   Instruction Decode
  //   F
  //   CLA
  //   C
  //   ~B
  //   RAM DATA
  //   I1
  //   ~A
  //   I0
  //   LOAD
  //   AND
  //   OR
  //   XOR
  //   ADD
  //   SUB
  //   STORE
  //   JMP
  //   ACCUMULATOR
  //   U35B
  //   16 bit Shift Register A
  //   ENTER H
  //   Data Input
  //   OUTPUT REGISTER
  //   U30F
  //   ENTER L
  //   Clock Sequencer
  //   Mask Instr Field
  //   U24, U25, U26
  //   U27
  //   # Clock
  //   16 bit Shift Register B
  //   U24A
  //   U24B
  //   U27A
  //   U27B
  //   U27D
  //   CLR ACC
  //   Note Clock Inverted
  //   U28
  //   U27C
  //   U24C
  //   Carry is only set before Bit 0 of an operation
  //   Any residual carry is cleared before an operation
  //   Bit Serial ALU
  //   U24D
  //   U25D
  //   U25C
  //   U25B
  //   Zero B for
  //   Jump instructions
  //   U35C
  //   Latch Result
  //   Write Result to RAM
  //   Increment PC
  //   Read Instruction from ROM
  //   Latch Instruction and MAR Address/Data
  //   Load B Register from Bus
  //   Set Carry
  //   U26B
  //   U26C
  //   U26A
  //   Suppress Carry
  //   U22
  //   U30
  //   U26D
  //   U25A
  //   Carry FF
endmodule
