// Digital circuit spider_3.dig as structural Verilog
module spider_3 (
  input  clk,
  input  in_4,
  input  in_5,
  input  in_6,
  input  in_7,
  output GCLK,
  output Fout
);

  wire _8_n16, A0, A1, A2, A3, A4, A5, A6, A7, A8, A9, A10, A11, A12, A13, A14, ADD, AND, and_1_out, Aout,
       Bout, BUS0, BUS1, BUS2, BUS3, BUS4, BUS5, BUS6, BUS7, button_1_out, button_2_out, button_3_out,
       button_4_out, button_5_out, button_6_out, button_7_out, button_8_out, button_9_out, button_10_out,
       button_11_out, button_12_out, button_13_out, button_14_out, button_15_out, button_16_out,
       button_17_out, button_18_out, C, Cin, CLA, CLR, Cout, D0, D1, D2, D3, D4, D5, D6, D7, D8, D9, D10,
       D11, D12, D13, D14, D15, d_ff_1_nq, d_ff_2_nq, d_ff_3_nq, d_ff_4_nq, d_ff_5_nq, d_ff_6_nq, d_ff_7_nq,
       d_ff_8_nq, d_ff_9_nq, d_ff_10_nq, d_ff_11_nq, d_ff_12_nq, diodebackward_4_out, diodebackward_9_out,
       diodebackward_11_out, diodebackward_13_out, diodeforward_1_out, F, I0, I1, IC13_pin9, IC14_pin9,
       IC16_2_nq, IC16_nq, IC17_2_nq, IC17_nq, IX, LD, LDH, LDL, nA, nand_2_out, nand_5_out, nand_6_out,
       nand_7_out, nand_8_out, nand_11_out, nand_12_out, nand_13_out, nand_14_out, nand_15_out, nand_16_out,
       nand_17_out, nB, nClr, nCLRPC, nJMP, nLD, nSet, nZERO, OR, pullup_1_out, pullup_2_out, pullup_5_out,
       pullup_6_out, Q0, Q1, Q2, Q3, Q4, Q5, Q6, Q7, RES, RST, SETC, SUB, SW, T0, U2_pin9, U2_pin10,
       U2_pin11, U2_pin12, U2_pin13, U2_pin14, U2_pin15, U3_pin9, U7_pin15, U16_pin18, U17_pin15, XOR,
       xor_1_out, xor_2_out, xor_3_out, xor_4_out;
  wire [3:0] IC13_pin3, IC13_pin7, U5_pin6, U5_pin13, U6_pin6, U7_pin11;
  wire [3:1] U6_pin10;

  _74138 U1 (
    .pin1(in_4), .pin2(in_5), .pin3(in_6), .pin4(in_7), .pin5(1'b0), .pin6(1'b1), .pin7(SW), .pin8(1'b0),
    .pin9(SUB), .pin10(ADD), .pin11(XOR), .pin12(OR), .pin13(AND), .pin14(LDH), .pin15(LDL), .pin16(1'b1));
  _74138 U2 (
    .pin1(in_4), .pin2(in_5), .pin3(in_6), .pin4(1'b0), .pin5(1'b0), .pin6(in_7), .pin7(nJMP), .pin8(1'b0),
    .pin9(U2_pin9), .pin10(U2_pin10), .pin11(U2_pin11), .pin12(U2_pin12), .pin13(U2_pin13), .pin14(U2_pin14),
    .pin15(U2_pin15), .pin16(1'b1));
  PullUp pullup_1 (.out(pullup_1_out));
  DiodeBackward diodebackward_1 (.in(LDL), .out(pullup_1_out));
  DiodeBackward diodebackward_2 (.in(SW), .out(pullup_1_out));
  PullUp pullup_2 (.out(pullup_2_out));
  DiodeBackward diodebackward_3 (.in(LDL), .out(pullup_2_out));
  DiodeBackward diodebackward_4 (.in(LDL), .out(diodebackward_4_out));
  DiodeBackward diodebackward_5 (.in(ADD), .out(diodebackward_4_out));
  DiodeBackward diodebackward_6 (.in(SUB), .out(diodebackward_4_out));
  DiodeBackward diodebackward_7 (.in(SW), .out(diodebackward_4_out));
  DiodeBackward diodebackward_8 (.in(nJMP), .out(diodebackward_4_out));
  PullUp pullup_3 (.out(diodebackward_4_out));
  DiodeBackward diodebackward_9 (.in(SUB), .out(diodebackward_9_out));
  PullUp pullup_4 (.out(diodebackward_9_out));
  PullUp pullup_5 (.out(pullup_5_out));
  DiodeBackward diodebackward_10 (.in(SUB), .out(pullup_5_out));
  PullUp pullup_6 (.out(pullup_6_out));
  DiodeBackward diodebackward_11 (.in(AND), .out(diodebackward_11_out));
  DiodeBackward diodebackward_12 (.in(OR), .out(diodebackward_11_out));
  PullUp pullup_7 (.out(diodebackward_11_out));
  DiodeBackward diodebackward_13 (.in(LDL), .out(diodebackward_13_out));
  DiodeBackward diodebackward_14 (.in(LDH), .out(diodebackward_13_out));
  DiodeBackward diodebackward_15 (.in(OR), .out(diodebackward_13_out));
  DiodeBackward diodebackward_16 (.in(XOR), .out(diodebackward_13_out));
  DiodeBackward diodebackward_17 (.in(ADD), .out(diodebackward_13_out));
  DiodeBackward diodebackward_18 (.in(SUB), .out(diodebackward_13_out));
  DiodeBackward diodebackward_19 (.in(SW), .out(diodebackward_13_out));
  PullUp pullup_8 (.out(diodebackward_13_out));
  _74540 U2_2 (
    .pin1(1'b0), .pin2(diodebackward_13_out), .pin3(diodebackward_11_out), .pin4(pullup_6_out),
    .pin5(pullup_5_out), .pin6(diodebackward_9_out), .pin7(diodebackward_4_out), .pin8(pullup_2_out),
    .pin9(pullup_1_out), .pin10(1'b0), .pin11(_8_n16), .pin12(CLA), .pin13(F), .pin14(C), .pin15(nB),
    .pin16(nA), .pin17(I1), .pin18(I0), .pin19(1'b0), .pin20(1'b1));
  LED led_1 (.in(D15));
  D_FF IC17 (.D(IC17_nq), .C(button_1_out), .Q(D15), .nQ(IC17_nq));
  Button button_1 (.out(button_1_out));
  _74165 U3 (
    .pin1(LD), .pin2(GCLK), .pin3(D11), .pin4(D10), .pin5(D9), .pin6(D8), .pin8(1'b0), .pin9(U3_pin9),
    .pin10(1'b0), .pin11(D15), .pin12(D14), .pin13(D13), .pin14(D12), .pin15(1'b0), .pin16(1'b1));  // open: pin7
  LED led_2 (.in(D14));
  D_FF d_ff_1 (.D(d_ff_1_nq), .C(button_2_out), .Q(D14), .nQ(d_ff_1_nq));
  Button button_2 (.out(button_2_out));
  LED led_3 (.in(D13));
  D_FF d_ff_2 (.D(d_ff_2_nq), .C(button_3_out), .Q(D13), .nQ(d_ff_2_nq));
  Button button_3 (.out(button_3_out));
  _74595 IC13 (
    .pin1(IC13_pin3[2]), .pin2(IC13_pin3[1]), .pin3(IC13_pin3[0]), .pin4(IC13_pin7[3]), .pin5(IC13_pin7[2]),
    .pin6(IC13_pin7[1]), .pin7(IC13_pin7[0]), .pin8(1'b0), .pin9(IC13_pin9), .pin10(RES), .pin11(GCLK),
    .pin12(T0), .pin13(1'b0), .pin14(Fout), .pin15(IC13_pin3[3]), .pin16(1'b1));
  LED led_4 (.in(D12));
  D_FF d_ff_3 (.D(d_ff_3_nq), .C(button_4_out), .Q(D12), .nQ(d_ff_3_nq));
  Button button_4 (.out(button_4_out));
  LED led_5 (.in(D11));
  D_FF d_ff_4 (.D(d_ff_4_nq), .C(button_5_out), .Q(D11), .nQ(d_ff_4_nq));
  Button button_5 (.out(button_5_out));
  LED led_6 (.in(D10));
  D_FF d_ff_5 (.D(d_ff_5_nq), .C(button_6_out), .Q(D10), .nQ(d_ff_5_nq));
  Button button_6 (.out(button_6_out));
  _74165 U4 (
    .pin1(LD), .pin2(GCLK), .pin3(D3), .pin4(D2), .pin5(D1), .pin6(D0), .pin8(1'b0), .pin9(Bout),
    .pin10(U3_pin9), .pin11(D7), .pin12(D6), .pin13(D5), .pin14(D4), .pin15(1'b0), .pin16(1'b1));  // open: pin7
  LED led_7 (.in(D9));
  D_FF d_ff_6 (.D(d_ff_6_nq), .C(button_7_out), .Q(D9), .nQ(d_ff_6_nq));
  Button button_7 (.out(button_7_out));
  LED led_8 (.in(D8));
  D_FF IC17_2 (.D(IC17_2_nq), .C(button_8_out), .Q(D8), .nQ(IC17_2_nq));
  Button button_8 (.out(button_8_out));
  _74595 IC14 (
    .pin1(BUS6), .pin2(BUS5), .pin3(BUS4), .pin4(BUS3), .pin5(BUS2), .pin6(BUS1), .pin7(BUS0), .pin8(1'b0),
    .pin9(IC14_pin9), .pin10(RES), .pin11(GCLK), .pin12(T0), .pin13(1'b0), .pin14(IC13_pin9), .pin15(BUS7),
    .pin16(1'b1));
  Seven_Seg_Hex seven_seg_hex_1 (.d({D15, D14, D13, D12}), .dp(1'b0));
  Seven_Seg_Hex seven_seg_hex_2 (.d({D11, D10, D9, D8}), .dp(1'b0));
  LED led_9 (.in(D7));
  D_FF IC16 (.D(IC16_nq), .C(button_9_out), .Q(D7), .nQ(IC16_nq));
  DiodeForward diodeforward_1 (.in(IC13_pin3[3]), .out(diodeforward_1_out));
  DiodeForward diodeforward_2 (.in(IC13_pin3[2]), .out(diodeforward_1_out));
  DiodeForward diodeforward_3 (.in(IC13_pin3[1]), .out(diodeforward_1_out));
  DiodeForward diodeforward_4 (.in(IC13_pin3[0]), .out(diodeforward_1_out));
  DiodeForward diodeforward_5 (.in(IC13_pin7[3]), .out(diodeforward_1_out));
  DiodeForward diodeforward_6 (.in(IC13_pin7[2]), .out(diodeforward_1_out));
  DiodeForward diodeforward_7 (.in(IC13_pin7[1]), .out(diodeforward_1_out));
  DiodeForward diodeforward_8 (.in(IC13_pin7[0]), .out(diodeforward_1_out));
  DiodeForward diodeforward_9 (.in(BUS7), .out(diodeforward_1_out));
  DiodeForward diodeforward_10 (.in(BUS6), .out(diodeforward_1_out));
  DiodeForward diodeforward_11 (.in(BUS5), .out(diodeforward_1_out));
  DiodeForward diodeforward_12 (.in(BUS4), .out(diodeforward_1_out));
  DiodeForward diodeforward_13 (.in(BUS3), .out(diodeforward_1_out));
  DiodeForward diodeforward_14 (.in(BUS2), .out(diodeforward_1_out));
  DiodeForward diodeforward_15 (.in(BUS1), .out(diodeforward_1_out));
  DiodeForward diodeforward_16 (.in(BUS0), .out(diodeforward_1_out));
  LED led_10 (.in(D6));
  D_FF d_ff_7 (.D(d_ff_7_nq), .C(button_10_out), .Q(D6), .nQ(d_ff_7_nq));
  Button button_9 (.out(button_9_out));
  Seven_Seg_Hex seven_seg_hex_3 (.d(IC13_pin3), .dp(1'b0));
  LED led_11 (.in(diodeforward_1_out));
  PullDown pulldown_1 (.out(diodeforward_1_out));
  LED led_12 (.in(D5));
  D_FF d_ff_8 (.D(d_ff_8_nq), .C(button_11_out), .Q(D5), .nQ(d_ff_8_nq));
  Button button_10 (.out(button_10_out));
  Seven_Seg_Hex seven_seg_hex_4 (.d(IC13_pin7), .dp(1'b0));
  LED led_13 (.in(D4));
  D_FF d_ff_9 (.D(d_ff_9_nq), .C(button_12_out), .Q(D4), .nQ(d_ff_9_nq));
  Button button_11 (.out(button_11_out));
  Seven_Seg_Hex seven_seg_hex_5 (.d({BUS7, BUS6, BUS5, BUS4}), .dp(1'b0));
  nand nand_1 (nZERO, diodeforward_1_out, diodeforward_1_out);
  _74164 U5 (
    .pin1(1'b1), .pin2(Fout), .pin3(U5_pin6[3]), .pin4(U5_pin6[2]), .pin5(U5_pin6[1]), .pin6(U5_pin6[0]),
    .pin7(1'b0), .pin8(GCLK), .pin9(CLR), .pin10(U5_pin13[3]), .pin11(U5_pin13[2]), .pin12(U5_pin13[1]),
    .pin13(U5_pin13[0]), .pin14(1'b1));
  LED led_14 (.in(D3));
  D_FF d_ff_10 (.D(d_ff_10_nq), .C(button_13_out), .Q(D3), .nQ(d_ff_10_nq));
  Button button_12 (.out(button_12_out));
  Seven_Seg_Hex seven_seg_hex_6 (.d({BUS3, BUS2, BUS1, BUS0}), .dp(1'b0));
  LED led_15 (.in(D2));
  D_FF d_ff_11 (.D(d_ff_11_nq), .C(button_14_out), .Q(D2), .nQ(d_ff_11_nq));
  Button button_13 (.out(button_13_out));
  LED led_16 (.in(D1));
  D_FF d_ff_12 (.D(d_ff_12_nq), .C(button_15_out), .Q(D1), .nQ(d_ff_12_nq));
  Button button_14 (.out(button_14_out));
  Seven_Seg_Hex seven_seg_hex_7 (.d(U5_pin6), .dp(1'b0));
  LED led_17 (.in(D0));
  D_FF IC16_2 (.D(IC16_2_nq), .C(button_16_out), .Q(D0), .nQ(IC16_2_nq));
  Button button_15 (.out(button_15_out));
  Seven_Seg_Hex seven_seg_hex_8 (.d(U5_pin13), .dp(1'b0));
  Button button_16 (.out(button_16_out));
  Seven_Seg_Hex seven_seg_hex_9 (.d({A7, A6, A5, A4}), .dp(1'b0));
  Seven_Seg_Hex seven_seg_hex_10 (.d(U6_pin6), .dp(1'b0));
  Seven_Seg_Hex seven_seg_hex_11 (.d({D7, D6, D5, D4}), .dp(1'b0));
  Seven_Seg_Hex seven_seg_hex_12 (.d({A3, A2, A1, A0}), .dp(1'b0));
  Seven_Seg_Hex seven_seg_hex_13 (.d({U6_pin10, Aout}), .dp(1'b0));
  _74164 U6 (
    .pin1(1'b1), .pin2(U5_pin13[0]), .pin3(U6_pin6[3]), .pin4(U6_pin6[2]), .pin5(U6_pin6[1]),
    .pin6(U6_pin6[0]), .pin7(1'b0), .pin8(GCLK), .pin9(CLR), .pin10(U6_pin10[3]), .pin11(U6_pin10[2]),
    .pin12(U6_pin10[1]), .pin13(Aout), .pin14(1'b1));
  Seven_Seg_Hex seven_seg_hex_14 (.d({D3, D2, D1, D0}), .dp(1'b0));
  Monoflop monoflop_1 (.C(button_17_out), .R(1'b0), .Q(nLD), .nQ(LD));
  Button button_17 (.out(button_17_out));
  _74541 U15 (
    .pin1(1'b1), .pin2(1'b0), .pin3(1'b0), .pin4(1'b0), .pin5(1'b0), .pin6(1'b0), .pin7(1'b0), .pin8(1'b0),
    .pin9(1'b0), .pin10(1'b0), .pin11(BUS0), .pin12(BUS1), .pin13(BUS2), .pin14(BUS3), .pin15(BUS4),
    .pin16(BUS5), .pin17(BUS6), .pin18(BUS7), .pin19(1'b1), .pin20(1'b1));
  Monoflop monoflop_2 (.C(LD), .R(1'b0), .Q(SETC), .nQ(RES));
  _74161 U7 (
    .pin1(RST), .pin2(clk), .pin3(1'b0), .pin4(1'b0), .pin5(1'b0), .pin6(1'b0), .pin7(1'b1), .pin8(1'b0),
    .pin9(1'b1), .pin10(1'b1), .pin11(U7_pin11[3]), .pin12(U7_pin11[2]), .pin13(U7_pin11[1]),
    .pin14(U7_pin11[0]), .pin15(U7_pin15), .pin16(1'b1));
  Monoflop monoflop_3 (.C(button_18_out), .R(1'b0), .nQ(nCLRPC));  // open: Q
  Button button_18 (.out(button_18_out));
  _74541 U16 (
    .pin1(1'b0), .pin2(1'b0), .pin3(1'b0), .pin4(1'b0), .pin5(1'b0), .pin6(1'b0), .pin7(1'b0), .pin8(1'b0),
    .pin9(1'b0), .pin10(1'b0), .pin11(A8), .pin12(A9), .pin13(A10), .pin14(A11), .pin15(A12), .pin16(A13),
    .pin17(A14), .pin18(U16_pin18), .pin19(1'b0), .pin20(1'b1));
  nand nand_2 (nand_2_out, _8_n16, _8_n16);
  nand nand_3 (nSet, SETC, C);
  or or_1 (nClr, C, LD);
  nand nand_4 (CLR, CLA, nLD);
  and and_1 (and_1_out, U7_pin11[0], U7_pin11[1], U7_pin11[2]);
  Seven_Seg_Hex seven_seg_hex_15 (.d(U7_pin11), .dp(1'b0));
  xor xor_1 (xor_1_out, Aout, nA);
  xor xor_2 (xor_2_out, nB, Bout);
  nand nand_5 (nand_5_out, U7_pin15, nand_2_out);
  nand nand_6 (nand_6_out, _8_n16, and_1_out);
  D_FF d_ff_13 (.D(nand_8_out), .C(clk), .Q(IX), .nQ(T0));
  nand nand_7 (nand_7_out, clk, clk);
  xor xor_3 (xor_3_out, xor_1_out, xor_2_out);
  nand nand_8 (nand_8_out, nand_5_out, nand_6_out);
  _74163 U17 (
    .pin1(nCLRPC), .pin2(clk), .pin3(BUS0), .pin4(BUS1), .pin5(BUS2), .pin6(BUS3), .pin7(IX), .pin8(1'b0),
    .pin9(nJMP), .pin10(1'b1), .pin11(A3), .pin12(A2), .pin13(A1), .pin14(A0), .pin15(U17_pin15), .pin16(1'b1));
  _74163 U16_2 (
    .pin1(nCLRPC), .pin2(clk), .pin3(BUS4), .pin4(BUS5), .pin5(BUS6), .pin6(BUS7), .pin7(IX), .pin8(1'b0),
    .pin9(nJMP), .pin10(U17_pin15), .pin11(A7), .pin12(A6), .pin13(A5), .pin14(A4), .pin16(1'b1));  // open: pin15
  nand nand_9 (GCLK, nand_7_out, RST);
  nand nand_10 (RST, RES, nand_11_out);
  nand nand_11 (nand_11_out, RST, T0);
  xor xor_4 (xor_4_out, xor_3_out, Cin);
  nand nand_12 (nand_12_out, xor_3_out, Cin);
  nand nand_13 (nand_13_out, xor_1_out, xor_2_out);
  nand nand_14 (nand_14_out, nand_12_out, nand_13_out);
  nand nand_15 (nand_15_out, xor_4_out, I0);
  nand nand_16 (nand_16_out, I1, nand_14_out);
  nand nand_17 (nand_17_out, nand_14_out, F);
  _74574 _74574_1 (
    .pin1(1'b0), .pin2(Fout), .pin3(Q0), .pin4(Q1), .pin5(Q2), .pin6(Q3), .pin7(Q4), .pin8(Q5), .pin9(Q6),
    .pin10(1'b0), .pin11(GCLK), .pin12(Q7), .pin13(Q6), .pin14(Q5), .pin15(Q4), .pin16(Q3), .pin17(Q2),
    .pin18(Q1), .pin19(Q0), .pin20(1'b1));
  nand nand_18 (Fout, nand_15_out, nand_16_out);
  nand nand_19 (Cout, nand_17_out, nand_17_out);
  _62256 U36 (
    .A0(A0), .A1(A1), .A2(A2), .A3(A3), .A4(A4), .A5(A5), .A6(A6), .A7(A7), .A8(A8), .A9(A9), .A10(A10),
    .A11(A11), .A12(A12), .nCE(1'b0), .nOE(1'b1), .nWE(1'b1), .D0(BUS0), .D1(BUS1), .D2(BUS2), .D3(BUS3),
    .D4(BUS4), .D5(BUS5), .D6(BUS6), .D7(BUS7), .VCC(1'b1), .GND(1'b0), .A13(A13), .A14(A14));
  Seven_Seg_Hex seven_seg_hex_16 (.d({Q0, Q1, Q2, Q3}), .dp(1'b0));
  Seven_Seg_Hex seven_seg_hex_17 (.d({Q4, Q5, Q6, Q7}), .dp(1'b0));
  D_FF_AS d_ff_as_1 (.Set(~nSet), .D(Cout), .C(GCLK), .Clr(~nClr), .Q(Cin));  // open: nQ

  // Notes on the sheet:
  //   clk: Hz: 16
  //   Instruction Input
  //   8/~16
  //   Instruction Decode
  //   CLA
  //   F
  //   ~B
  //   C
  //   ~A
  //   I1
  //   I0
  //   LD-H
  //   LD-L
  //   AND
  //   OR
  //   XOR
  //   ADD
  //   SUB
  //   SWAP
  //   JMP
  //   16 bit Shift Register B
  //   Output Display Registers
  //   ENTER H
  //   SPIDER Bit serial CPU
  //   Data Input
  //   ENTER L
  //   16 bit Shift Register A
  //   ACCUMULATOR
  //   PC LOW
  //   LOAD
  //   Acc to Bus
  //   8 or 16-bit sequence
  //   CLR PC
  //   High Address
  //   Clock Sequencer
  //   CLR ACC
  //   # Clock
  //   Carry is only set before Bit 0 of an operation
  //   Any residual carry is cleared before an operation
  //   Suppress Carry
  //   32K RAM
  //   OUTPUT
  //   Carry FF
endmodule
