// Digital circuit spider_5.dig as structural Verilog
module spider_5 (
  input  clk,
  input  in_4,
  input  in_5,
  input  in_6,
  input  in_7,
  input  in_8,
  input  in_9,
  input  in_10,
  input  in_11,
  input  nRD_WR,
  output GCLK,
  output Fout
);

  wire _8_n16, A0, A1, A2, A3, A4, A5, A6, A7, A8, A9, A10, A11, A12, A13, A14, A15, ADD, AND, and_1_out,
       Aout, Bin, Bout, BUS0, BUS1, BUS2, BUS3, BUS4, BUS5, BUS6, BUS7, button_1_out, button_2_out,
       button_3_out, button_4_out, button_5_out, button_6_out, button_7_out, button_8_out, button_9_out,
       button_10_out, button_11_out, button_12_out, button_13_out, button_14_out, button_15_out,
       button_16_out, button_17_out, button_18_out, C, Cin, CLA, CLKB, CLKC, CLKD, CLKE, CLKM, CLKX, CLKY,
       CLR, Cout, D0, D1, D2, D3, D4, D5, D6, D7, D8, D9, D10, D11, D12, D13, D14, D15, d_ff_1_nq, d_ff_2_nq,
       d_ff_3_nq, d_ff_4_nq, d_ff_5_nq, d_ff_6_nq, d_ff_7_nq, d_ff_8_nq, d_ff_9_nq, d_ff_10_nq, d_ff_11_nq,
       d_ff_12_nq, diodebackward_1_out, diodebackward_6_out, diodebackward_9_out, diodebackward_10_out, F,
       I0, I1, IC16_2_nq, IC16_nq, IC17_2_nq, IC17_nq, IC23_pin9, IC25_pin9, IX, LD, LDH, LDL, M0, M1, M2,
       M3, M4, M5, M6, M7, Mout, nA, nand_1_out, nand_2_out, nand_3_out, nand_4_out, nand_5_out, nand_7_out,
       nand_11_out, nand_12_out, nand_13_out, nand_14_out, nand_15_out, nand_16_out, nand_17_out,
       nand_18_out, nand_19_out, nand_25_out, nand_26_out, nand_27_out, nand_28_out, nand_29_out,
       nand_30_out, nand_31_out, nand_32_out, nand_35_out, nand_36_out, nand_37_out, nand_38_out, nB, nClr,
       nCLRPC, nJMP, nLD, nLO_HI, nSet, nWE, nWEH, nWEL, OR, PC_Cin, PCin, PCout, pullup_1_out, pullup_3_out,
       pullup_6_out, pullup_7_out, RES, Rout, RST, SELB, SELM, SELX, SELY, SETC, Sout, SUB, SW, T0, U2_pin9,
       U2_pin10, U2_pin11, U2_pin12, U2_pin13, U2_pin14, U2_pin15, U3_pin9, U5_pin9, U7_2_pin15, Xin, XOR,
       xor_1_out, xor_2_out, xor_3_out, xor_4_out, xor_5_out, Xout, Yin, Yout;
  wire [2:0] U7_2_pin14;
  wire [3:0] U5_2_pin6, U5_2_pin13, U6_2_pin6, U7_pin3, U7_pin10, U8_pin3, U9_pin6, U9_pin13, U10_pin6;
  wire [3:1] U6_2_pin10, U8_pin10, U10_pin10;

  _74138 _74138_1 (
    .pin1(in_8), .pin2(in_9), .pin3(in_10), .pin4(GCLK), .pin5(1'b0), .pin6(1'b1), .pin7(CLKE), .pin8(1'b0),
    .pin9(CLKD), .pin10(CLKC), .pin11(CLKB), .pin12(CLKM), .pin13(CLKY), .pin14(CLKX), .pin16(1'b1));  // open: pin15
  _74138 _74138_2 (
    .pin1(in_8), .pin2(in_9), .pin3(in_10), .pin4(1'b0), .pin5(1'b0), .pin6(1'b1), .pin8(1'b0), .pin11(SELB),
    .pin12(SELM), .pin13(SELY), .pin14(SELX), .pin16(1'b1));  // open: pin7, pin9, pin10, pin15
  _74151 _74151_1 (
    .pin1(Mout), .pin2(Yout), .pin3(Xout), .pin4(Sout), .pin5(Rout), .pin7(1'b0), .pin8(1'b0), .pin9(in_10),
    .pin10(in_9), .pin11(in_8), .pin12(1'b0), .pin13(1'b0), .pin14(1'b0), .pin15(Bout), .pin16(1'b1));  // open: pin6
  xor xor_1 (xor_1_out, PCout, PC_Cin);
  nand nand_1 (nand_1_out, PCout, PC_Cin);
  _74595 IC23 (
    .pin1(A14), .pin2(A13), .pin3(A12), .pin4(A11), .pin5(A10), .pin6(A9), .pin7(A8), .pin8(1'b0),
    .pin9(IC23_pin9), .pin10(nCLRPC), .pin11(GCLK), .pin12(T0), .pin13(1'b0), .pin14(PCin), .pin15(A15),
    .pin16(1'b1));
  nand nand_2 (nand_2_out, in_11, in_11);
  nand nand_3 (nand_3_out, nand_1_out, nand_1_out);
  _74138 U2 (
    .pin1(in_4), .pin2(in_5), .pin3(in_6), .pin4(1'b0), .pin5(1'b0), .pin6(in_7), .pin7(nJMP), .pin8(1'b0),
    .pin9(U2_pin9), .pin10(U2_pin10), .pin11(U2_pin11), .pin12(U2_pin12), .pin13(U2_pin13), .pin14(U2_pin14),
    .pin15(U2_pin15), .pin16(1'b1));
  nand nand_4 (nand_4_out, xor_1_out, nand_2_out);
  nand nand_5 (nand_5_out, in_11, Rout);
  _74138 U1 (
    .pin1(in_4), .pin2(in_5), .pin3(in_6), .pin4(in_7), .pin5(1'b0), .pin6(1'b1), .pin7(SW), .pin8(1'b0),
    .pin9(SUB), .pin10(ADD), .pin11(XOR), .pin12(OR), .pin13(AND), .pin14(LDH), .pin15(LDL), .pin16(1'b1));
  _74595 IC24 (
    .pin1(A6), .pin2(A5), .pin3(A4), .pin4(A3), .pin5(A2), .pin6(A1), .pin7(A0), .pin8(1'b0), .pin9(PCout),
    .pin10(nCLRPC), .pin11(GCLK), .pin12(T0), .pin13(1'b0), .pin14(IC23_pin9), .pin15(A7), .pin16(1'b1));
  nand nand_6 (PCin, nand_4_out, nand_5_out);
  D_FF_AS d_ff_as_1 (.Set(~LD), .D(nand_3_out), .C(GCLK), .Clr(~1'b1), .Q(PC_Cin));  // open: nQ
  DiodeBackward diodebackward_1 (.in(SW), .out(diodebackward_1_out));
  PullUp pullup_1 (.out(pullup_1_out));
  PullUp pullup_2 (.out(diodebackward_1_out));
  DiodeBackward diodebackward_2 (.in(LDL), .out(pullup_1_out));
  Seven_Seg_Hex seven_seg_hex_1 (.d({A15, A14, A13, A12}), .dp(1'b0));
  PullUp pullup_3 (.out(pullup_3_out));
  DiodeBackward diodebackward_3 (.in(LDL), .out(pullup_3_out));
  DiodeBackward diodebackward_4 (.in(ADD), .out(pullup_3_out));
  DiodeBackward diodebackward_5 (.in(SUB), .out(pullup_3_out));
  DiodeBackward diodebackward_6 (.in(SUB), .out(diodebackward_6_out));
  DiodeBackward diodebackward_7 (.in(SW), .out(pullup_3_out));
  DiodeBackward diodebackward_8 (.in(nJMP), .out(pullup_3_out));
  Seven_Seg_Hex seven_seg_hex_2 (.d({A11, A10, A9, A8}), .dp(1'b0));
  Seven_Seg_Hex seven_seg_hex_3 (.d({A15, A14, A13, A12}), .dp(1'b0));
  PullUp pullup_4 (.out(diodebackward_6_out));
  DiodeBackward diodebackward_9 (.in(SUB), .out(diodebackward_9_out));
  Seven_Seg_Hex seven_seg_hex_4 (.d({A7, A6, A5, A4}), .dp(1'b0));
  Seven_Seg_Hex seven_seg_hex_5 (.d({A11, A10, A9, A8}), .dp(1'b0));
  PullUp pullup_5 (.out(diodebackward_9_out));
  PullUp pullup_6 (.out(pullup_6_out));
  Seven_Seg_Hex seven_seg_hex_6 (.d({A3, A2, A1, A0}), .dp(1'b0));
  Seven_Seg_Hex seven_seg_hex_7 (.d({A7, A6, A5, A4}), .dp(1'b0));
  PullUp pullup_7 (.out(pullup_7_out));
  DiodeBackward diodebackward_10 (.in(LDL), .out(diodebackward_10_out));
  DiodeBackward diodebackward_11 (.in(LDH), .out(diodebackward_10_out));
  DiodeBackward diodebackward_12 (.in(AND), .out(pullup_7_out));
  DiodeBackward diodebackward_13 (.in(OR), .out(diodebackward_10_out));
  DiodeBackward diodebackward_14 (.in(OR), .out(pullup_7_out));
  DiodeBackward diodebackward_15 (.in(XOR), .out(diodebackward_10_out));
  DiodeBackward diodebackward_16 (.in(ADD), .out(diodebackward_10_out));
  DiodeBackward diodebackward_17 (.in(SUB), .out(diodebackward_10_out));
  DiodeBackward diodebackward_18 (.in(SW), .out(diodebackward_10_out));
  Seven_Seg_Hex seven_seg_hex_8 (.d({A3, A2, A1, A0}), .dp(1'b0));
  PullUp pullup_8 (.out(diodebackward_10_out));
  _74540 U2_2 (
    .pin1(1'b0), .pin2(diodebackward_10_out), .pin3(pullup_7_out), .pin4(pullup_6_out),
    .pin5(diodebackward_9_out), .pin6(diodebackward_6_out), .pin7(pullup_3_out), .pin8(pullup_1_out),
    .pin9(diodebackward_1_out), .pin10(1'b0), .pin11(_8_n16), .pin12(CLA), .pin13(F), .pin14(C), .pin15(nB),
    .pin16(nA), .pin17(I1), .pin18(I0), .pin19(1'b0), .pin20(1'b1));
  Seven_Seg_Hex seven_seg_hex_9 (.d({BUS7, BUS6, BUS5, BUS4}), .dp(1'b0));
  _74165 U5 (
    .pin1(LD), .pin2(CLKM), .pin3(BUS3), .pin4(BUS2), .pin5(BUS1), .pin6(BUS0), .pin8(1'b0), .pin9(U5_pin9),
    .pin10(1'b0), .pin11(BUS7), .pin12(BUS6), .pin13(BUS5), .pin14(BUS4), .pin15(1'b0), .pin16(1'b1));  // open: pin7
  Seven_Seg_Hex seven_seg_hex_10 (.d({BUS3, BUS2, BUS1, BUS0}), .dp(1'b0));
  Seven_Seg_Hex seven_seg_hex_11 (.d({M7, M6, M5, M4}), .dp(1'b0));
  Seven_Seg_Hex seven_seg_hex_12 (.d({M3, M2, M1, M0}), .dp(1'b0));
  LED led_1 (.in(D15));
  D_FF IC17 (.D(IC17_nq), .C(button_1_out), .Q(D15), .nQ(IC17_nq));
  Button button_1 (.out(button_1_out));
  _74165 U3 (
    .pin1(LD), .pin2(GCLK), .pin3(D11), .pin4(D10), .pin5(D9), .pin6(D8), .pin8(1'b0), .pin9(U3_pin9),
    .pin10(1'b0), .pin11(D15), .pin12(D14), .pin13(D13), .pin14(D12), .pin15(1'b0), .pin16(1'b1));  // open: pin7
  LED led_2 (.in(D14));
  D_FF d_ff_1 (.D(d_ff_1_nq), .C(button_2_out), .Q(D14), .nQ(d_ff_1_nq));
  Button button_2 (.out(button_2_out));
  _74165 U6 (
    .pin1(LD), .pin2(CLKM), .pin3(M3), .pin4(M2), .pin5(M1), .pin6(M0), .pin8(1'b0), .pin9(Mout),
    .pin10(U5_pin9), .pin11(M7), .pin12(M6), .pin13(M5), .pin14(M4), .pin15(1'b0), .pin16(1'b1));  // open: pin7
  LED led_3 (.in(D13));
  D_FF d_ff_2 (.D(d_ff_2_nq), .C(button_3_out), .Q(D13), .nQ(d_ff_2_nq));
  Button button_3 (.out(button_3_out));
  _74164 U7 (
    .pin1(1'b1), .pin2(Xin), .pin3(U7_pin3[3]), .pin4(U7_pin3[2]), .pin5(U7_pin3[1]), .pin6(U7_pin3[0]),
    .pin7(1'b0), .pin8(CLKX), .pin9(nCLRPC), .pin10(U7_pin10[3]), .pin11(U7_pin10[2]), .pin12(U7_pin10[1]),
    .pin13(U7_pin10[0]), .pin14(1'b1));
  LED led_4 (.in(D12));
  D_FF d_ff_3 (.D(d_ff_3_nq), .C(button_4_out), .Q(D12), .nQ(d_ff_3_nq));
  Button button_4 (.out(button_4_out));
  LED led_5 (.in(D11));
  D_FF d_ff_4 (.D(d_ff_4_nq), .C(button_5_out), .Q(D11), .nQ(d_ff_4_nq));
  Button button_5 (.out(button_5_out));
  LED led_6 (.in(D10));
  D_FF d_ff_5 (.D(d_ff_5_nq), .C(button_6_out), .Q(D10), .nQ(d_ff_5_nq));
  Button button_6 (.out(button_6_out));
  Seven_Seg_Hex seven_seg_hex_13 (.d(U7_pin3), .dp(1'b0));
  _74165 U4 (
    .pin1(LD), .pin2(GCLK), .pin3(D3), .pin4(D2), .pin5(D1), .pin6(D0), .pin8(1'b0), .pin9(Sout),
    .pin10(U3_pin9), .pin11(D7), .pin12(D6), .pin13(D5), .pin14(D4), .pin15(1'b0), .pin16(1'b1));  // open: pin7
  LED led_7 (.in(D9));
  D_FF d_ff_6 (.D(d_ff_6_nq), .C(button_7_out), .Q(D9), .nQ(d_ff_6_nq));
  Button button_7 (.out(button_7_out));
  Seven_Seg_Hex seven_seg_hex_14 (.d(U7_pin10), .dp(1'b0));
  LED led_8 (.in(D8));
  D_FF IC17_2 (.D(IC17_2_nq), .C(button_8_out), .Q(D8), .nQ(IC17_2_nq));
  Button button_8 (.out(button_8_out));
  Seven_Seg_Hex seven_seg_hex_15 (.d(U8_pin3), .dp(1'b0));
  Seven_Seg_Hex seven_seg_hex_16 (.d({D15, D14, D13, D12}), .dp(1'b0));
  _62256 U36 (
    .A0(nLO_HI), .A1(A1), .A2(A2), .A3(A3), .A4(A4), .A5(A5), .A6(A6), .A7(A7), .A8(A8), .A9(A9), .A10(A10),
    .A11(A11), .A12(A12), .nCE(1'b0), .nOE(nRD_WR), .nWE(nWE), .D0(BUS0), .D1(BUS1), .D2(BUS2), .D3(BUS3),
    .D4(BUS4), .D5(BUS5), .D6(BUS6), .D7(BUS7), .VCC(1'b1), .GND(1'b0), .A13(A13), .A14(A14));
  Seven_Seg_Hex seven_seg_hex_17 (.d({U8_pin10, Xout}), .dp(1'b0));
  _74164 U8 (
    .pin1(1'b1), .pin2(U7_pin10[0]), .pin3(U8_pin3[3]), .pin4(U8_pin3[2]), .pin5(U8_pin3[1]),
    .pin6(U8_pin3[0]), .pin7(1'b0), .pin8(CLKX), .pin9(nCLRPC), .pin10(U8_pin10[3]), .pin11(U8_pin10[2]),
    .pin12(U8_pin10[1]), .pin13(Xout), .pin14(1'b1));
  Seven_Seg_Hex seven_seg_hex_18 (.d({D11, D10, D9, D8}), .dp(1'b0));
  LED led_9 (.in(D7));
  D_FF IC16 (.D(IC16_nq), .C(button_9_out), .Q(D7), .nQ(IC16_nq));
  LED led_10 (.in(D6));
  D_FF d_ff_7 (.D(d_ff_7_nq), .C(button_10_out), .Q(D6), .nQ(d_ff_7_nq));
  Button button_9 (.out(button_9_out));
  LED led_11 (.in(D5));
  D_FF d_ff_8 (.D(d_ff_8_nq), .C(button_11_out), .Q(D5), .nQ(d_ff_8_nq));
  Button button_10 (.out(button_10_out));
  LED led_12 (.in(D4));
  D_FF d_ff_9 (.D(d_ff_9_nq), .C(button_12_out), .Q(D4), .nQ(d_ff_9_nq));
  Button button_11 (.out(button_11_out));
  LED led_13 (.in(D3));
  D_FF d_ff_10 (.D(d_ff_10_nq), .C(button_13_out), .Q(D3), .nQ(d_ff_10_nq));
  Button button_12 (.out(button_12_out));
  _74573 _74573_1 (
    .pin1(1'b0), .pin2(BUS0), .pin3(BUS1), .pin4(BUS2), .pin5(BUS3), .pin6(BUS4), .pin7(BUS5), .pin8(BUS6),
    .pin9(BUS7), .pin10(1'b0), .pin11(nLO_HI), .pin12(M7), .pin13(M6), .pin14(M5), .pin15(M4), .pin16(M3),
    .pin17(M2), .pin18(M1), .pin19(M0), .pin20(1'b1));
  nand nand_7 (nand_7_out, nLO_HI, nLO_HI);
  _74164 U9 (
    .pin1(1'b1), .pin2(Yin), .pin3(U9_pin6[3]), .pin4(U9_pin6[2]), .pin5(U9_pin6[1]), .pin6(U9_pin6[0]),
    .pin7(1'b0), .pin8(CLKY), .pin9(nCLRPC), .pin10(U9_pin13[3]), .pin11(U9_pin13[2]), .pin12(U9_pin13[1]),
    .pin13(U9_pin13[0]), .pin14(1'b1));
  _74164 U5_2 (
    .pin1(1'b1), .pin2(Fout), .pin3(U5_2_pin6[3]), .pin4(U5_2_pin6[2]), .pin5(U5_2_pin6[1]),
    .pin6(U5_2_pin6[0]), .pin7(1'b0), .pin8(GCLK), .pin9(CLR), .pin10(U5_2_pin13[3]), .pin11(U5_2_pin13[2]),
    .pin12(U5_2_pin13[1]), .pin13(U5_2_pin13[0]), .pin14(1'b1));
  LED led_14 (.in(D2));
  D_FF d_ff_11 (.D(d_ff_11_nq), .C(button_14_out), .Q(D2), .nQ(d_ff_11_nq));
  Button button_13 (.out(button_13_out));
  nand nand_8 (nWEL, nRD_WR, nLO_HI);
  nand nand_9 (nWEH, nRD_WR, nand_7_out);
  LED led_15 (.in(D1));
  D_FF d_ff_12 (.D(d_ff_12_nq), .C(button_15_out), .Q(D1), .nQ(d_ff_12_nq));
  Button button_14 (.out(button_14_out));
  LED led_16 (.in(D0));
  D_FF IC16_2 (.D(IC16_2_nq), .C(button_16_out), .Q(D0), .nQ(IC16_2_nq));
  Button button_15 (.out(button_15_out));
  Seven_Seg_Hex seven_seg_hex_19 (.d(U9_pin6), .dp(1'b0));
  Seven_Seg_Hex seven_seg_hex_20 (.d(U5_2_pin6), .dp(1'b0));
  Button button_16 (.out(button_16_out));
  nand nand_10 (nWE, nRD_WR, nRD_WR);
  Seven_Seg_Hex seven_seg_hex_21 (.d(U9_pin13), .dp(1'b0));
  Seven_Seg_Hex seven_seg_hex_22 (.d(U5_2_pin13), .dp(1'b0));
  Seven_Seg_Hex seven_seg_hex_23 (.d({D7, D6, D5, D4}), .dp(1'b0));
  Seven_Seg_Hex seven_seg_hex_24 (.d(U10_pin6), .dp(1'b0));
  Seven_Seg_Hex seven_seg_hex_25 (.d(U6_2_pin6), .dp(1'b0));
  Seven_Seg_Hex seven_seg_hex_26 (.d({D3, D2, D1, D0}), .dp(1'b0));
  Seven_Seg_Hex seven_seg_hex_27 (.d({U10_pin10, Yout}), .dp(1'b0));
  Seven_Seg_Hex seven_seg_hex_28 (.d({U6_2_pin10, Aout}), .dp(1'b0));
  nand nand_11 (nand_11_out, SELX, SELX);
  nand nand_12 (nand_12_out, SELY, SELY);
  nand nand_13 (nand_13_out, SELB, SELB);
  _74164 U10 (
    .pin1(1'b1), .pin2(U9_pin13[0]), .pin3(U10_pin6[3]), .pin4(U10_pin6[2]), .pin5(U10_pin6[1]),
    .pin6(U10_pin6[0]), .pin7(1'b0), .pin8(CLKY), .pin9(nCLRPC), .pin10(U10_pin10[3]), .pin11(U10_pin10[2]),
    .pin12(U10_pin10[1]), .pin13(Yout), .pin14(1'b1));
  _74164 U6_2 (
    .pin1(1'b1), .pin2(U5_2_pin13[0]), .pin3(U6_2_pin6[3]), .pin4(U6_2_pin6[2]), .pin5(U6_2_pin6[1]),
    .pin6(U6_2_pin6[0]), .pin7(1'b0), .pin8(GCLK), .pin9(CLR), .pin10(U6_2_pin10[3]), .pin11(U6_2_pin10[2]),
    .pin12(U6_2_pin10[1]), .pin13(Aout), .pin14(1'b1));
  Monoflop monoflop_1 (.C(button_17_out), .R(1'b0), .Q(nLD), .nQ(LD));
  Button button_17 (.out(button_17_out));
  nand nand_14 (nand_14_out, Xout, SELX);
  nand nand_15 (nand_15_out, nand_11_out, Fout);
  nand nand_16 (nand_16_out, Yout, SELY);
  nand nand_17 (nand_17_out, nand_12_out, Fout);
  nand nand_18 (nand_18_out, Bout, SELB);
  nand nand_19 (nand_19_out, nand_13_out, Fout);
  Monoflop monoflop_2 (.C(LD), .R(1'b0), .Q(SETC), .nQ(RES));
  nand nand_20 (Xin, nand_14_out, nand_15_out);
  nand nand_21 (Yin, nand_16_out, nand_17_out);
  nand nand_22 (Bin, nand_18_out, nand_19_out);
  Monoflop monoflop_3 (.C(button_18_out), .R(1'b0), .nQ(nCLRPC));  // open: Q
  Button button_18 (.out(button_18_out));
  _74595 IC25 (
    .pin1(BUS6), .pin2(BUS5), .pin3(BUS4), .pin4(BUS3), .pin5(BUS2), .pin6(BUS1), .pin7(BUS0), .pin8(1'b0),
    .pin9(IC25_pin9), .pin10(nCLRPC), .pin11(CLKB), .pin12(T0), .pin13(nWEL), .pin14(Bin), .pin15(BUS7),
    .pin16(1'b1));
  nand nand_23 (nSet, SETC, C);
  or or_1 (nClr, C, LD);
  nand nand_24 (CLR, CLA, nLD);
  _74161 U7_2 (
    .pin1(RST), .pin2(clk), .pin3(1'b0), .pin4(1'b0), .pin5(1'b0), .pin6(1'b0), .pin7(1'b1), .pin8(1'b0),
    .pin9(1'b1), .pin10(1'b1), .pin11(nLO_HI), .pin12(U7_2_pin14[2]), .pin13(U7_2_pin14[1]),
    .pin14(U7_2_pin14[0]), .pin15(U7_2_pin15), .pin16(1'b1));
  xor xor_2 (xor_2_out, Aout, nA);
  xor xor_3 (xor_3_out, nB, Rout);
  xor xor_4 (xor_4_out, xor_2_out, xor_3_out);
  nand nand_25 (nand_25_out, _8_n16, _8_n16);
  and and_1 (and_1_out, U7_2_pin14[0], U7_2_pin14[1], U7_2_pin14[2]);
  _74595 IC26 (
    .pin1(BUS6), .pin2(BUS5), .pin3(BUS4), .pin4(BUS3), .pin5(BUS2), .pin6(BUS1), .pin7(BUS0), .pin8(1'b0),
    .pin9(Bout), .pin10(nCLRPC), .pin11(CLKB), .pin12(T0), .pin13(nWEH), .pin14(IC25_pin9), .pin15(BUS7),
    .pin16(1'b1));
  Seven_Seg_Hex seven_seg_hex_29 (.d({nLO_HI, U7_2_pin14}), .dp(1'b0));
  xor xor_5 (xor_5_out, xor_4_out, Cin);
  nand nand_26 (nand_26_out, xor_4_out, Cin);
  nand nand_27 (nand_27_out, xor_2_out, xor_3_out);
  nand nand_28 (nand_28_out, U7_2_pin15, nand_25_out);
  nand nand_29 (nand_29_out, _8_n16, and_1_out);
  nand nand_30 (nand_30_out, clk, clk);
  nand nand_31 (nand_31_out, nand_26_out, nand_27_out);
  nand nand_32 (nand_32_out, nand_28_out, nand_29_out);
  Seven_Seg_Hex seven_seg_hex_30 (.d({BUS7, BUS6, BUS5, BUS4}), .dp(1'b0));
  nand nand_33 (GCLK, nand_30_out, RST);
  nand nand_34 (RST, RES, nand_35_out);
  nand nand_35 (nand_35_out, RST, T0);
  Seven_Seg_Hex seven_seg_hex_31 (.d({BUS3, BUS2, BUS1, BUS0}), .dp(1'b0));
  Seven_Seg_Hex seven_seg_hex_32 (.d({BUS7, BUS6, BUS5, BUS4}), .dp(1'b0));
  nand nand_36 (nand_36_out, xor_5_out, I0);
  nand nand_37 (nand_37_out, I1, nand_31_out);
  nand nand_38 (nand_38_out, nand_31_out, F);
  D_FF d_ff_13 (.D(nand_32_out), .C(clk), .Q(IX), .nQ(T0));
  Seven_Seg_Hex seven_seg_hex_33 (.d({BUS3, BUS2, BUS1, BUS0}), .dp(1'b0));
  nand nand_39 (Fout, nand_36_out, nand_37_out);
  nand nand_40 (Cout, nand_38_out, nand_38_out);
  D_FF_AS d_ff_as_2 (.Set(~nSet), .D(Cout), .C(GCLK), .Clr(~nClr), .Q(Cin));  // open: nQ

  // Other names for the same wires on the sheet: nINC_LD = in_11; nOE = nRD_WR; nRRES = nCLRPC

  // Notes on the sheet:
  //   clk: Hz: 2147483647
  //   SPIder Bit Serial CPU
  //   Register Select
  //   Instruction Input
  //   Carry is only set before Bit 0 of an operation
  //   Carry FF
  //   8/~16
  //   Instruction Decode
  //   CLA
  //   Program Counter
  //   F
  //   PC HI
  //   C
  //   ~A
  //   ~B
  //   PC LOW
  //   I1
  //   I0
  //   LD-H
  //   LD-L
  //   AND
  //   OR
  //   XOR
  //   ADD
  //   SUB
  //   SWAP
  //   JMP
  //   BUS DATA
  //   16 bit Switch Register S
  //   ENTER H
  //   X REGISTER
  //   Data Input
  //   32K RAM
  //   ENTER L
  //   16 bit Shift Register A
  //   Y REGISTER
  //   ACCUMULATOR
  //   LOAD
  //   CLR PC
  //   CLR ACC
  //   Any residual carry is cleared before an operation
  //   8 or 16-bit sequence
  //   # Clock
  //   Clock Sequencer
  //   Suppress Carry
endmodule
