// Digital circuit spider_7.dig as structural Verilog
module spider_7 (
  input  clk,
  input  nRD_WR,
  output Fout
);

  wire _8_n16, A0, A1, A2, A3, A4, A5, A6, A7, A8, A9, A10, A11, A12, A13, A14, A15, Ac0, Ac1, Ac2, Ac3, Ac4,
       Ac5, Ac6, Ac7, Ac8, Ac9, Ac10, Ac11, Ac12, Ac13, Ac14, Ac15, ADD, AND, Bin, Bout, BUS0, BUS1, BUS2,
       BUS3, BUS4, BUS5, BUS6, BUS7, BUS8, BUS9, BUS10, BUS11, BUS12, BUS13, BUS14, BUS15, button_1_out,
       button_2_out, button_3_out, button_4_out, button_5_out, button_6_out, button_7_out, button_8_out,
       button_9_out, button_10_out, button_11_out, button_12_out, button_13_out, button_14_out,
       button_15_out, button_16_out, button_17_out, button_18_out, C, Cin, CLA, CLKB, CLKC, CLKD, CLKE, CLKM,
       CLKX, CLKY, CLR, Cout, D0, D1, D2, D3, D4, D5, D6, D7, D8, D9, D10, D11, D12, D13, D14, D15,
       d_ff_1_nq, d_ff_2_nq, d_ff_3_nq, d_ff_4_nq, d_ff_5_nq, d_ff_6_nq, d_ff_7_nq, d_ff_8_nq, d_ff_9_nq,
       d_ff_10_nq, d_ff_11_nq, d_ff_12_nq, diodebackward_1_out, diodebackward_2_out, diodebackward_3_out,
       diodebackward_4_out, diodebackward_10_out, diodebackward_13_out, diodebackward_14_out,
       diodeforward_1_out, Dout, F, GCLK, I0, I1, IC16_2_nq, IC16_nq, IC17_2_nq, IC17_nq, IR0, IR1, IR2, IR3,
       IR4, IR5, IR6, IR7, IX, LD, LDH, LDL, Mout, nA, nand_1_out, nand_2_out, nand_3_out, nand_4_out,
       nand_5_out, nand_7_out, nand_8_out, nand_9_out, nand_10_out, nand_11_out, nand_12_out, nand_13_out,
       nand_14_out, nand_15_out, nand_21_out, nand_24_out, nand_25_out, nand_26_out, nand_27_out,
       nand_30_out, nand_31_out, nand_32_out, nand_33_out, nB, nClr, nCLRPC, nINC_LD, nJMP, nLD, nLH, nLL,
       nSet, nWE, nZERO, OR, PC_Cin, PCin, PCout, pullup_1_out, pullup_2_out, pullup_3_out, pullup_6_out,
       pullup_7_out, pullup_9_out, pullup_11_out, pullup_14_out, pullup_15_out, R0, R1, R2, R3, R4, R5, R6,
       R7, RES, RMA, RMB, Rout, RST, S0, S1, S2, S3, S4, S5, S6, S7, S8, S9, S10, S11, S12, S13, S14, S15,
       SELB, SELM, SELX, SELY, SETC, Sout, SUB, SW, T0, U2_pin9, U2_pin10, U2_pin11, U2_pin12, U2_pin13,
       U2_pin14, U2_pin15, U2A_pin11, U2A_pin12, U2A_pin13, U2A_pin14, U2A_pin15, U3_pin9, U5_pin9, U11_pin9,
       U16_pin9, U20_pin15, U37_pin9, Xin, XOR, xor_1_out, xor_2_out, xor_3_out, xor_4_out, xor_5_out, Xout,
       Yin, Yout;
  wire [3:0] U7_pin3, U7_pin10, U8_pin3, U9_pin6, U9_pin13, U10_pin6, U20_pin14;
  wire [3:1] U8_pin10, U10_pin10;

  _27C1024 U33 (
    .nCE(1'b0), .nOE(1'b0), .VPP(1'b1), .VDD(1'b1), .GND(1'b0), .I_O0(R0), .I_O1(R1), .I_O2(R2), .I_O3(R3),
    .I_O4(R4), .I_O5(R5), .I_O6(R6), .I_O7(R7), .A0(A0), .A1(A1), .A2(A2), .A3(A3), .A4(A4), .A5(A5),
    .A6(A6), .A7(A7), .A8(A8), .A9(A9), .A10(A10), .A11(A11), .A12(A12), .A13(A13), .A14(A14), .A15(A15),
    .I_O8(IR0), .I_O9(IR1), .I_O10(IR2), .I_O11(IR3), .I_O12(IR4), .I_O13(IR5), .I_O14(IR6), .I_O15(IR7),
    .VSS(1'b0));
  _74165 U37 (
    .pin1(LD), .pin2(GCLK), .pin3(D11), .pin4(D10), .pin5(D9), .pin6(D8), .pin8(1'b0), .pin9(U37_pin9),
    .pin10(1'b0), .pin11(D15), .pin12(D14), .pin13(D13), .pin14(D12), .pin15(1'b0), .pin16(1'b1));  // open: pin7
  _74541 U39 (
    .pin1(nLH), .pin2(R0), .pin3(R1), .pin4(R2), .pin5(R3), .pin6(R4), .pin7(R5), .pin8(R6), .pin9(R7),
    .pin10(1'b0), .pin11(D15), .pin12(D14), .pin13(D13), .pin14(D12), .pin15(D11), .pin16(D10), .pin17(D9),
    .pin18(D8), .pin19(1'b0), .pin20(1'b1));
  _74541 U40 (
    .pin1(nLL), .pin2(R0), .pin3(R1), .pin4(R2), .pin5(R3), .pin6(R4), .pin7(R5), .pin8(R6), .pin9(R7),
    .pin10(1'b0), .pin11(D7), .pin12(D6), .pin13(D5), .pin14(D4), .pin15(D3), .pin16(D2), .pin17(D1),
    .pin18(D0), .pin19(1'b0), .pin20(1'b1));
  _74165 U38 (
    .pin1(LD), .pin2(GCLK), .pin3(D3), .pin4(D2), .pin5(D1), .pin6(D0), .pin8(1'b0), .pin9(Dout),
    .pin10(U37_pin9), .pin11(D7), .pin12(D6), .pin13(D5), .pin14(D4), .pin15(1'b0), .pin16(1'b1));  // open: pin7
  PullDown pulldown_1 (.out(D15));
  PullDown pulldown_2 (.out(D7));
  PullDown pulldown_3 (.out(D13));
  PullDown pulldown_4 (.out(D14));
  PullDown pulldown_5 (.out(D5));
  PullDown pulldown_6 (.out(D6));
  PullDown pulldown_7 (.out(D11));
  PullDown pulldown_8 (.out(D12));
  PullDown pulldown_9 (.out(D3));
  PullDown pulldown_10 (.out(D4));
  Seven_Seg_Hex seven_seg_hex_1 (.d({IR7, IR6, IR5, IR4}), .dp(1'b0));
  PullDown pulldown_11 (.out(D10));
  PullDown pulldown_12 (.out(D9));
  PullDown pulldown_13 (.out(D2));
  PullDown pulldown_14 (.out(D1));
  Seven_Seg_Hex seven_seg_hex_2 (.d({IR3, IR2, IR1, IR0}), .dp(1'b0));
  PullDown pulldown_15 (.out(D8));
  PullDown pulldown_16 (.out(D0));
  Seven_Seg_Hex seven_seg_hex_3 (.d({R7, R6, R5, R4}), .dp(1'b0));
  _74541 U36 (
    .pin1(1'b1), .pin2(R0), .pin3(R1), .pin4(R2), .pin5(R3), .pin6(R4), .pin7(R5), .pin8(R6), .pin9(R7),
    .pin10(1'b0), .pin11(BUS7), .pin12(BUS6), .pin13(BUS5), .pin14(BUS4), .pin15(BUS3), .pin16(BUS2),
    .pin17(BUS1), .pin18(BUS0), .pin19(1'b1), .pin20(1'b1));
  Seven_Seg_Hex seven_seg_hex_4 (.d({R3, R2, R1, R0}), .dp(1'b0));
  LED IND (.in(IR3));
  _74595 U16 (
    .pin1(A14), .pin2(A13), .pin3(A12), .pin4(A11), .pin5(A10), .pin6(A9), .pin7(A8), .pin8(1'b0),
    .pin9(U16_pin9), .pin10(nCLRPC), .pin11(GCLK), .pin12(T0), .pin13(1'b0), .pin14(PCin), .pin15(A15),
    .pin16(1'b1));
  _74138 U1 (
    .pin1(IR4), .pin2(IR5), .pin3(IR6), .pin4(IR7), .pin5(1'b0), .pin6(1'b1), .pin7(SW), .pin8(1'b0),
    .pin9(SUB), .pin10(ADD), .pin11(XOR), .pin12(OR), .pin13(AND), .pin14(LDH), .pin15(LDL), .pin16(1'b1));
  _74138 U2 (
    .pin1(IR4), .pin2(IR5), .pin3(IR6), .pin4(1'b0), .pin5(1'b0), .pin6(IR7), .pin7(nJMP), .pin8(1'b0),
    .pin9(U2_pin9), .pin10(U2_pin10), .pin11(U2_pin11), .pin12(U2_pin12), .pin13(U2_pin13), .pin14(U2_pin14),
    .pin15(U2_pin15), .pin16(1'b1));
  _74138 U13 (
    .pin1(IR0), .pin2(IR1), .pin3(IR2), .pin4(GCLK), .pin5(1'b0), .pin6(1'b1), .pin7(CLKE), .pin8(1'b0),
    .pin9(CLKD), .pin10(CLKC), .pin11(CLKB), .pin12(CLKM), .pin13(CLKY), .pin14(CLKX), .pin16(1'b1));  // open: pin15
  _74138 U14 (
    .pin1(IR0), .pin2(IR1), .pin3(IR2), .pin4(1'b0), .pin5(1'b0), .pin6(1'b1), .pin8(1'b0), .pin11(SELB),
    .pin12(SELM), .pin13(SELY), .pin14(SELX), .pin16(1'b1));  // open: pin7, pin9, pin10, pin15
  _74151 U15 (
    .pin1(Mout), .pin2(Yout), .pin3(Xout), .pin4(Dout), .pin5(Rout), .pin7(1'b0), .pin8(1'b0), .pin9(IR2),
    .pin10(IR1), .pin11(IR0), .pin12(1'b0), .pin13(1'b0), .pin14(Sout), .pin15(Bout), .pin16(1'b1));  // open: pin6
  xor xor_1 (xor_1_out, PCout, PC_Cin);
  nand nand_1 (nand_1_out, PCout, PC_Cin);
  _74595 U17 (
    .pin1(A6), .pin2(A5), .pin3(A4), .pin4(A3), .pin5(A2), .pin6(A1), .pin7(A0), .pin8(1'b0), .pin9(PCout),
    .pin10(nCLRPC), .pin11(GCLK), .pin12(T0), .pin13(1'b0), .pin14(U16_pin9), .pin15(A7), .pin16(1'b1));
  nand nand_2 (nand_2_out, nINC_LD, nINC_LD);
  nand nand_3 (nand_3_out, nand_1_out, nand_1_out);
  PullUp pullup_1 (.out(pullup_1_out));
  PullUp pullup_2 (.out(pullup_2_out));
  PullUp pullup_3 (.out(pullup_3_out));
  DiodeBackward diodebackward_1 (.in(LDH), .out(diodebackward_1_out));
  nand nand_4 (nand_4_out, xor_1_out, nand_2_out);
  nand nand_5 (nand_5_out, nINC_LD, Rout);
  PullUp pullup_4 (.out(diodebackward_1_out));
  DiodeBackward diodebackward_2 (.in(LDL), .out(diodebackward_2_out));
  nand nand_6 (PCin, nand_4_out, nand_5_out);
  PullUp pullup_5 (.out(diodebackward_2_out));
  PullUp pullup_6 (.out(pullup_6_out));
  Seven_Seg_Hex seven_seg_hex_5 (.d({A15, A14, A13, A12}), .dp(1'b0));
  D_FF_AS d_ff_as_1 (.Set(~LD), .D(nand_3_out), .C(GCLK), .Clr(~1'b1), .Q(PC_Cin));  // open: nQ
  PullUp pullup_7 (.out(pullup_7_out));
  DiodeBackward diodebackward_3 (.in(U2_pin15), .out(diodebackward_3_out));
  Seven_Seg_Hex seven_seg_hex_6 (.d({A11, A10, A9, A8}), .dp(1'b0));
  PullUp pullup_8 (.out(diodebackward_3_out));
  DiodeBackward diodebackward_4 (.in(SW), .out(diodebackward_4_out));
  Seven_Seg_Hex seven_seg_hex_7 (.d({A7, A6, A5, A4}), .dp(1'b0));
  PullUp pullup_9 (.out(pullup_9_out));
  PullUp pullup_10 (.out(diodebackward_4_out));
  DiodeBackward diodebackward_5 (.in(LDL), .out(pullup_9_out));
  Seven_Seg_Hex seven_seg_hex_8 (.d({A3, A2, A1, A0}), .dp(1'b0));
  PullUp pullup_11 (.out(pullup_11_out));
  DiodeBackward diodebackward_6 (.in(LDL), .out(pullup_11_out));
  DiodeBackward diodebackward_7 (.in(LDH), .out(pullup_11_out));
  DiodeBackward diodebackward_8 (.in(ADD), .out(pullup_11_out));
  DiodeBackward diodebackward_9 (.in(SUB), .out(pullup_11_out));
  DiodeBackward diodebackward_10 (.in(SUB), .out(diodebackward_10_out));
  DiodeBackward diodebackward_11 (.in(SW), .out(pullup_11_out));
  DiodeBackward diodebackward_12 (.in(nJMP), .out(pullup_11_out));
  Seven_Seg_Hex seven_seg_hex_9 (.d({A15, A14, A13, A12}), .dp(1'b0));
  PullUp pullup_12 (.out(diodebackward_10_out));
  DiodeBackward diodebackward_13 (.in(SUB), .out(diodebackward_13_out));
  _74165 U5 (
    .pin1(LD), .pin2(CLKM), .pin3(BUS11), .pin4(BUS10), .pin5(BUS9), .pin6(BUS8), .pin8(1'b0),
    .pin9(U5_pin9), .pin10(1'b0), .pin11(BUS15), .pin12(BUS14), .pin13(BUS13), .pin14(BUS12), .pin15(1'b0),
    .pin16(1'b1));  // open: pin7
  Seven_Seg_Hex seven_seg_hex_10 (.d({A11, A10, A9, A8}), .dp(1'b0));
  PullUp pullup_13 (.out(diodebackward_13_out));
  PullUp pullup_14 (.out(pullup_14_out));
  Seven_Seg_Hex seven_seg_hex_11 (.d({A7, A6, A5, A4}), .dp(1'b0));
  PullUp pullup_15 (.out(pullup_15_out));
  DiodeBackward diodebackward_14 (.in(LDL), .out(diodebackward_14_out));
  DiodeBackward diodebackward_15 (.in(LDH), .out(diodebackward_14_out));
  DiodeBackward diodebackward_16 (.in(AND), .out(pullup_15_out));
  DiodeBackward diodebackward_17 (.in(OR), .out(diodebackward_14_out));
  DiodeBackward diodebackward_18 (.in(OR), .out(pullup_15_out));
  DiodeBackward diodebackward_19 (.in(XOR), .out(diodebackward_14_out));
  DiodeBackward diodebackward_20 (.in(ADD), .out(diodebackward_14_out));
  DiodeBackward diodebackward_21 (.in(SUB), .out(diodebackward_14_out));
  DiodeBackward diodebackward_22 (.in(SW), .out(diodebackward_14_out));
  Seven_Seg_Hex seven_seg_hex_12 (.d({A3, A2, A1, A0}), .dp(1'b0));
  PullUp pullup_16 (.out(diodebackward_14_out));
  _74540 U2_2 (
    .pin1(1'b0), .pin2(diodebackward_14_out), .pin3(pullup_15_out), .pin4(pullup_14_out),
    .pin5(diodebackward_13_out), .pin6(diodebackward_10_out), .pin7(pullup_11_out), .pin8(pullup_9_out),
    .pin9(diodebackward_4_out), .pin10(1'b0), .pin11(_8_n16), .pin12(CLA), .pin13(F), .pin14(C), .pin15(nB),
    .pin16(nA), .pin17(I1), .pin18(I0), .pin19(1'b0), .pin20(1'b1));
  _74540 U2A (
    .pin1(1'b0), .pin2(diodebackward_3_out), .pin3(pullup_7_out), .pin4(pullup_6_out),
    .pin5(diodebackward_2_out), .pin6(diodebackward_1_out), .pin7(pullup_3_out), .pin8(pullup_1_out),
    .pin9(pullup_2_out), .pin10(1'b0), .pin11(U2A_pin11), .pin12(U2A_pin12), .pin13(U2A_pin13),
    .pin14(U2A_pin14), .pin15(U2A_pin15), .pin16(RMB), .pin17(RMA), .pin18(nINC_LD), .pin19(1'b0),
    .pin20(1'b1));
  Seven_Seg_Hex seven_seg_hex_13 (.d({BUS7, BUS6, BUS5, BUS4}), .dp(1'b0));
  Seven_Seg_Hex seven_seg_hex_14 (.d({BUS3, BUS2, BUS1, BUS0}), .dp(1'b0));
  _74165 U6 (
    .pin1(LD), .pin2(CLKM), .pin3(BUS3), .pin4(BUS2), .pin5(BUS1), .pin6(BUS0), .pin8(1'b0), .pin9(Mout),
    .pin10(U5_pin9), .pin11(BUS7), .pin12(BUS6), .pin13(BUS5), .pin14(BUS4), .pin15(1'b0), .pin16(1'b1));  // open: pin7
  Seven_Seg_Hex seven_seg_hex_15 (.d({BUS15, BUS14, BUS13, BUS12}), .dp(1'b0));
  not not_1 (nLL, U2A_pin15);
  not not_2 (nLH, U2A_pin14);
  Seven_Seg_Hex seven_seg_hex_16 (.d({BUS11, BUS10, BUS9, BUS8}), .dp(1'b0));
  LED led_1 (.in(S15));
  D_FF IC17 (.D(IC17_nq), .C(button_1_out), .Q(S15), .nQ(IC17_nq));
  Button button_1 (.out(button_1_out));
  _74165 U3 (
    .pin1(LD), .pin2(GCLK), .pin3(S11), .pin4(S10), .pin5(S9), .pin6(S8), .pin8(1'b0), .pin9(U3_pin9),
    .pin10(1'b0), .pin11(S15), .pin12(S14), .pin13(S13), .pin14(S12), .pin15(1'b0), .pin16(1'b1));  // open: pin7
  LED led_2 (.in(S14));
  D_FF d_ff_1 (.D(d_ff_1_nq), .C(button_2_out), .Q(S14), .nQ(d_ff_1_nq));
  Button button_2 (.out(button_2_out));
  LED led_3 (.in(S13));
  D_FF d_ff_2 (.D(d_ff_2_nq), .C(button_3_out), .Q(S13), .nQ(d_ff_2_nq));
  Button button_3 (.out(button_3_out));
  _74164 U7 (
    .pin1(1'b1), .pin2(Xin), .pin3(U7_pin3[3]), .pin4(U7_pin3[2]), .pin5(U7_pin3[1]), .pin6(U7_pin3[0]),
    .pin7(1'b0), .pin8(CLKX), .pin9(nCLRPC), .pin10(U7_pin10[3]), .pin11(U7_pin10[2]), .pin12(U7_pin10[1]),
    .pin13(U7_pin10[0]), .pin14(1'b1));
  LED led_4 (.in(S12));
  D_FF d_ff_3 (.D(d_ff_3_nq), .C(button_4_out), .Q(S12), .nQ(d_ff_3_nq));
  Button button_4 (.out(button_4_out));
  LED led_5 (.in(S11));
  D_FF d_ff_4 (.D(d_ff_4_nq), .C(button_5_out), .Q(S11), .nQ(d_ff_4_nq));
  Button button_5 (.out(button_5_out));
  _62256 U18 (
    .A0(A0), .A1(A1), .A2(A2), .A3(A3), .A4(A4), .A5(A5), .A6(A6), .A7(A7), .A8(A8), .A9(A9), .A10(A10),
    .A11(A11), .A12(A12), .nCE(1'b0), .nOE(nRD_WR), .nWE(nWE), .D0(BUS0), .D1(BUS1), .D2(BUS2), .D3(BUS3),
    .D4(BUS4), .D5(BUS5), .D6(BUS6), .D7(BUS7), .VCC(1'b1), .GND(1'b0), .A13(A13), .A14(A14));
  LED led_6 (.in(S10));
  D_FF d_ff_5 (.D(d_ff_5_nq), .C(button_6_out), .Q(S10), .nQ(d_ff_5_nq));
  Button button_6 (.out(button_6_out));
  Seven_Seg_Hex seven_seg_hex_17 (.d(U7_pin3), .dp(1'b0));
  _74165 U4 (
    .pin1(LD), .pin2(GCLK), .pin3(S3), .pin4(S2), .pin5(S1), .pin6(S0), .pin8(1'b0), .pin9(Sout),
    .pin10(U3_pin9), .pin11(S7), .pin12(S6), .pin13(S5), .pin14(S4), .pin15(1'b0), .pin16(1'b1));  // open: pin7
  LED led_7 (.in(S9));
  D_FF d_ff_6 (.D(d_ff_6_nq), .C(button_7_out), .Q(S9), .nQ(d_ff_6_nq));
  Button button_7 (.out(button_7_out));
  Seven_Seg_Hex seven_seg_hex_18 (.d(U7_pin10), .dp(1'b0));
  LED led_8 (.in(S8));
  D_FF IC17_2 (.D(IC17_2_nq), .C(button_8_out), .Q(S8), .nQ(IC17_2_nq));
  Button button_8 (.out(button_8_out));
  Seven_Seg_Hex seven_seg_hex_19 (.d(U8_pin3), .dp(1'b0));
  Seven_Seg_Hex seven_seg_hex_20 (.d({S15, S14, S13, S12}), .dp(1'b0));
  Seven_Seg_Hex seven_seg_hex_21 (.d({U8_pin10, Xout}), .dp(1'b0));
  _74164 U8 (
    .pin1(1'b1), .pin2(U7_pin10[0]), .pin3(U8_pin3[3]), .pin4(U8_pin3[2]), .pin5(U8_pin3[1]),
    .pin6(U8_pin3[0]), .pin7(1'b0), .pin8(CLKX), .pin9(nCLRPC), .pin10(U8_pin10[3]), .pin11(U8_pin10[2]),
    .pin12(U8_pin10[1]), .pin13(Xout), .pin14(1'b1));
  Seven_Seg_Hex seven_seg_hex_22 (.d({S11, S10, S9, S8}), .dp(1'b0));
  LED led_9 (.in(S7));
  D_FF IC16 (.D(IC16_nq), .C(button_9_out), .Q(S7), .nQ(IC16_nq));
  LED led_10 (.in(S6));
  D_FF d_ff_7 (.D(d_ff_7_nq), .C(button_10_out), .Q(S6), .nQ(d_ff_7_nq));
  Button button_9 (.out(button_9_out));
  _62256 U19 (
    .A0(A0), .A1(A1), .A2(A2), .A3(A3), .A4(A4), .A5(A5), .A6(A6), .A7(A7), .A8(A8), .A9(A9), .A10(A10),
    .A11(A11), .A12(A12), .nCE(1'b0), .nOE(nRD_WR), .nWE(nWE), .D0(BUS8), .D1(BUS9), .D2(BUS10), .D3(BUS11),
    .D4(BUS12), .D5(BUS13), .D6(BUS14), .D7(BUS15), .VCC(1'b1), .GND(1'b0), .A13(A13), .A14(A14));
  LED led_11 (.in(S5));
  D_FF d_ff_8 (.D(d_ff_8_nq), .C(button_11_out), .Q(S5), .nQ(d_ff_8_nq));
  Button button_10 (.out(button_10_out));
  LED led_12 (.in(S4));
  D_FF d_ff_9 (.D(d_ff_9_nq), .C(button_12_out), .Q(S4), .nQ(d_ff_9_nq));
  Button button_11 (.out(button_11_out));
  LED led_13 (.in(S3));
  D_FF d_ff_10 (.D(d_ff_10_nq), .C(button_13_out), .Q(S3), .nQ(d_ff_10_nq));
  Button button_12 (.out(button_12_out));
  _74164 U9 (
    .pin1(1'b1), .pin2(Yin), .pin3(U9_pin6[3]), .pin4(U9_pin6[2]), .pin5(U9_pin6[1]), .pin6(U9_pin6[0]),
    .pin7(1'b0), .pin8(CLKY), .pin9(nCLRPC), .pin10(U9_pin13[3]), .pin11(U9_pin13[2]), .pin12(U9_pin13[1]),
    .pin13(U9_pin13[0]), .pin14(1'b1));
  _74164 U5_2 (
    .pin1(1'b1), .pin2(Fout), .pin3(Ac15), .pin4(Ac14), .pin5(Ac13), .pin6(Ac12), .pin7(1'b0), .pin8(GCLK),
    .pin9(CLR), .pin10(Ac11), .pin11(Ac10), .pin12(Ac9), .pin13(Ac8), .pin14(1'b1));
  LED led_14 (.in(S2));
  D_FF d_ff_11 (.D(d_ff_11_nq), .C(button_14_out), .Q(S2), .nQ(d_ff_11_nq));
  Button button_13 (.out(button_13_out));
  LED led_15 (.in(S1));
  D_FF d_ff_12 (.D(d_ff_12_nq), .C(button_15_out), .Q(S1), .nQ(d_ff_12_nq));
  Button button_14 (.out(button_14_out));
  LED led_16 (.in(S0));
  D_FF IC16_2 (.D(IC16_2_nq), .C(button_16_out), .Q(S0), .nQ(IC16_2_nq));
  Button button_15 (.out(button_15_out));
  Seven_Seg_Hex seven_seg_hex_23 (.d(U9_pin6), .dp(1'b0));
  Seven_Seg_Hex seven_seg_hex_24 (.d({Ac15, Ac14, Ac13, Ac12}), .dp(1'b0));
  Button button_16 (.out(button_16_out));
  Seven_Seg_Hex seven_seg_hex_25 (.d(U9_pin13), .dp(1'b0));
  Seven_Seg_Hex seven_seg_hex_26 (.d({Ac11, Ac10, Ac9, Ac8}), .dp(1'b0));
  Seven_Seg_Hex seven_seg_hex_27 (.d({S7, S6, S5, S4}), .dp(1'b0));
  Seven_Seg_Hex seven_seg_hex_28 (.d(U10_pin6), .dp(1'b0));
  Seven_Seg_Hex seven_seg_hex_29 (.d({Ac7, Ac6, Ac5, Ac4}), .dp(1'b0));
  Seven_Seg_Hex seven_seg_hex_30 (.d({S3, S2, S1, S0}), .dp(1'b0));
  Seven_Seg_Hex seven_seg_hex_31 (.d({U10_pin10, Yout}), .dp(1'b0));
  Seven_Seg_Hex seven_seg_hex_32 (.d({Ac3, Ac2, Ac1, Ac0}), .dp(1'b0));
  _74164 U10 (
    .pin1(1'b1), .pin2(U9_pin13[0]), .pin3(U10_pin6[3]), .pin4(U10_pin6[2]), .pin5(U10_pin6[1]),
    .pin6(U10_pin6[0]), .pin7(1'b0), .pin8(CLKY), .pin9(nCLRPC), .pin10(U10_pin10[3]), .pin11(U10_pin10[2]),
    .pin12(U10_pin10[1]), .pin13(Yout), .pin14(1'b1));
  _74164 U6_2 (
    .pin1(1'b1), .pin2(Ac8), .pin3(Ac7), .pin4(Ac6), .pin5(Ac5), .pin6(Ac4), .pin7(1'b0), .pin8(GCLK),
    .pin9(CLR), .pin10(Ac3), .pin11(Ac2), .pin12(Ac1), .pin13(Ac0), .pin14(1'b1));
  Monoflop monoflop_1 (.C(button_17_out), .R(1'b0), .Q(nLD), .nQ(LD));
  Button button_17 (.out(button_17_out));
  nand nand_7 (nand_7_out, SELX, SELX);
  nand nand_8 (nand_8_out, SELY, SELY);
  nand nand_9 (nand_9_out, SELB, SELB);
  Monoflop monoflop_2 (.C(LD), .R(1'b0), .Q(SETC), .nQ(RES));
  nand nand_10 (nand_10_out, Xout, SELX);
  nand nand_11 (nand_11_out, nand_7_out, Fout);
  nand nand_12 (nand_12_out, Yout, SELY);
  nand nand_13 (nand_13_out, nand_8_out, Fout);
  nand nand_14 (nand_14_out, Bout, SELB);
  nand nand_15 (nand_15_out, nand_9_out, Fout);
  nand nand_16 (nWE, nRD_WR, nRD_WR);
  Monoflop monoflop_3 (.C(button_18_out), .R(1'b0), .nQ(nCLRPC));  // open: Q
  Button button_18 (.out(button_18_out));
  nand nand_17 (Xin, nand_10_out, nand_11_out);
  nand nand_18 (Yin, nand_12_out, nand_13_out);
  nand nand_19 (Bin, nand_14_out, nand_15_out);
  DiodeForward diodeforward_1 (.in(Ac15), .out(diodeforward_1_out));
  DiodeForward diodeforward_2 (.in(Ac14), .out(diodeforward_1_out));
  DiodeForward diodeforward_3 (.in(Ac13), .out(diodeforward_1_out));
  DiodeForward diodeforward_4 (.in(Ac12), .out(diodeforward_1_out));
  DiodeForward diodeforward_5 (.in(Ac11), .out(diodeforward_1_out));
  DiodeForward diodeforward_6 (.in(Ac10), .out(diodeforward_1_out));
  DiodeForward diodeforward_7 (.in(Ac9), .out(diodeforward_1_out));
  DiodeForward diodeforward_8 (.in(Ac8), .out(diodeforward_1_out));
  DiodeForward diodeforward_9 (.in(Ac7), .out(diodeforward_1_out));
  DiodeForward diodeforward_10 (.in(Ac6), .out(diodeforward_1_out));
  DiodeForward diodeforward_11 (.in(Ac5), .out(diodeforward_1_out));
  DiodeForward diodeforward_12 (.in(Ac4), .out(diodeforward_1_out));
  DiodeForward diodeforward_13 (.in(Ac3), .out(diodeforward_1_out));
  DiodeForward diodeforward_14 (.in(Ac2), .out(diodeforward_1_out));
  DiodeForward diodeforward_15 (.in(Ac1), .out(diodeforward_1_out));
  DiodeForward diodeforward_16 (.in(Ac0), .out(diodeforward_1_out));
  _74595 U11 (
    .pin1(BUS14), .pin2(BUS13), .pin3(BUS12), .pin4(BUS11), .pin5(BUS10), .pin6(BUS9), .pin7(BUS8),
    .pin8(1'b0), .pin9(U11_pin9), .pin10(nCLRPC), .pin11(CLKB), .pin12(T0), .pin13(nWE), .pin14(Bin),
    .pin15(BUS15), .pin16(1'b1));
  LED led_17 (.in(diodeforward_1_out));
  PullDown pulldown_17 (.out(diodeforward_1_out));
  nand nand_20 (nSet, SETC, C);
  nand nand_21 (nand_21_out, C, C);
  nand nand_22 (CLR, CLA, nLD);
  xor xor_2 (xor_2_out, Ac0, nA);
  xor xor_3 (xor_3_out, nB, Rout);
  _74161 U20 (
    .pin1(RST), .pin2(clk), .pin3(1'b0), .pin4(1'b0), .pin5(1'b0), .pin6(1'b0), .pin7(1'b1), .pin8(1'b0),
    .pin9(1'b1), .pin10(1'b1), .pin11(U20_pin14[3]), .pin12(U20_pin14[2]), .pin13(U20_pin14[1]),
    .pin14(U20_pin14[0]), .pin15(U20_pin15), .pin16(1'b1));
  D_FF d_ff_13 (.D(diodeforward_1_out), .C(T0), .nQ(nZERO));  // open: Q
  nand nand_23 (nClr, nand_21_out, nLD);
  Seven_Seg_Hex seven_seg_hex_33 (.d(U20_pin14), .dp(1'b0));
  xor xor_4 (xor_4_out, xor_2_out, xor_3_out);
  _74595 U12 (
    .pin1(BUS6), .pin2(BUS5), .pin3(BUS4), .pin4(BUS3), .pin5(BUS2), .pin6(BUS1), .pin7(BUS0), .pin8(1'b0),
    .pin9(Bout), .pin10(nCLRPC), .pin11(CLKB), .pin12(T0), .pin13(nWE), .pin14(U11_pin9), .pin15(BUS7),
    .pin16(1'b1));
  xor xor_5 (xor_5_out, xor_4_out, Cin);
  nand nand_24 (nand_24_out, xor_4_out, Cin);
  nand nand_25 (nand_25_out, xor_2_out, xor_3_out);
  D_FF d_ff_14 (.D(U20_pin15), .C(clk), .Q(IX), .nQ(T0));
  nand nand_26 (nand_26_out, clk, clk);
  nand nand_27 (nand_27_out, nand_24_out, nand_25_out);
  Seven_Seg_Hex seven_seg_hex_34 (.d({BUS15, BUS14, BUS13, BUS12}), .dp(1'b0));
  nand nand_28 (GCLK, nand_26_out, RST);
  nand nand_29 (RST, RES, nand_30_out);
  nand nand_30 (nand_30_out, RST, T0);
  Seven_Seg_Hex seven_seg_hex_35 (.d({BUS11, BUS10, BUS9, BUS8}), .dp(1'b0));
  Seven_Seg_Hex seven_seg_hex_36 (.d({BUS7, BUS6, BUS5, BUS4}), .dp(1'b0));
  nand nand_31 (nand_31_out, xor_5_out, I0);
  nand nand_32 (nand_32_out, I1, nand_27_out);
  nand nand_33 (nand_33_out, nand_27_out, F);
  Seven_Seg_Hex seven_seg_hex_37 (.d({BUS3, BUS2, BUS1, BUS0}), .dp(1'b0));
  nand nand_34 (Fout, nand_31_out, nand_32_out);
  nand nand_35 (Cout, nand_33_out, nand_33_out);
  D_FF_AS d_ff_as_2 (.Set(~nSet), .D(Cout), .C(GCLK), .Clr(~nClr), .Q(Cin));  // open: nQ

  // Other names for the same wires on the sheet: Aout = Ac0; PCLD = nINC_LD; nOE = nRD_WR; nRRES = nCLRPC

  // Notes on the sheet:
  //   clk: Hz: 2147483647
  //   Instruction ROM
  //   INSTRUCTION
  //   DATA
  //   SPIder Bit Serial CPU
  //   Instruction Input
  //   Register Select
  //   Carry is only set before Bit 0 of an operation
  //   U40A
  //   U24B
  //   U24C
  //   LL
  //   LH
  //   Program Counter
  //   RMB
  //   U31
  //   Carry FF
  //   RMA
  //   U32A
  //   8/~16
  //   PC
  //   Instruction Decode
  //   CLA
  //   F
  //   PC HI
  //   C
  //   ~A
  //   ~B
  //   Memory Read Register
  //   PC LOW
  //   I1
  //   I0
  //   LD-H
  //   LD-L
  //   AND
  //   OR
  //   XOR
  //   ADD
  //   SUB
  //   SWAP
  //   JMP
  //   BUS DATA
  //   16 bit Switch Register S
  //   ENTER H
  //   RAM LO
  //   X REGISTER
  //   Data Input
  //   RAM HI
  //   ENTER L
  //   16 bit Shift Register A
  //   Y REGISTER
  //   ACCUMULATOR
  //   LOAD
  //   CLR PC
  //   U24A
  //   U21
  //   U22
  //   U23
  //   Zero Detect
  //   CLR ACC
  //   Memory Write Register
  //   U30A
  //   U30B
  //   U30D
  //   U30C
  //   Clock #
  //   U26
  //   Any residual carry is cleared before an operation
  //   Clock Sequencer
  //   U29B
  //   U25A
  //   U27
  //   U25B
  //   U25C
  //   U25D
  //   Suppress Carry
  //   U28
  //   U29A
endmodule
